// Logisim project Pipeline_RISC_Processor.circ as structural Verilog: 1 circuit, main circuit main
module main (
  output [31:0] out_1,
  output [31:0] out_2,
  output [31:0] out_3,
  output [31:0] out_4,
  output [31:0] out_5,
  output [31:0] out_6,
  output [31:0] out_7,
  output [31:0] out_8,
  output [31:0] out_9,
  output [31:0] out_10,
  output [31:0] out_11,
  output [31:0] out_12,
  output [31:0] out_13,
  output [31:0] out_14,
  output [31:0] out_15,
  output [31:0] out_16,
  output [31:0] out_17,
  output [31:0] out_18,
  output [31:0] out_19,
  output [31:0] out_20,
  output [31:0] out_21,
  output [31:0] out_22,
  output [31:0] out_23,
  output [31:0] out_24,
  output [31:0] out_25,
  output [31:0] out_26,
  output [31:0] out_27,
  output [31:0] out_28,
  output [31:0] out_29,
  output [31:0] out_30,
  output [31:0] out_31,
  output [31:0] out_32,
  output [19:0] out_33
);

  wire ALU_ctrl, BEQ_BNE, BGEU, BLT, BLTU, BQE, Branch, CLK, JALR, Kill1, Kill2, main_11_out_12, Mem_Read,
       Mem_Read_K, Mem_Read_PL, Mem_Read_PL_1, MemWrite, MemWrite_K, MemWrite_PL, MemWrite_PL_1,
       MUX_Extender, MUX_Extender_K, MUX_Extender_PL, MUX_RD_1, MUX_RD_1_K, MUX_RD_1_PL, MUX_RD_1_PL_1,
       MUX_RD_2, MUX_RD_2_K, MUX_RD_2_PL, MUX_RD_2_PL_1, MUX_RS1_RD, MUX_SA_RS2, MUX_SA_RS2_K, MUX_SA_RS2_PL,
       or_1_out, RegWrite, RegWrite_K, RegWrite_PL, RegWrite_PL_1, RegWrite_PL_2, Signal_OF_ADD,
       Signal_OF_ADD_K, Signal_OF_ADD_PL, Signal_OF_SUB, Signal_OF_SUB_K, Signal_OF_SUB_PL, Stall;
  wire [1:0] ALU_op, ALU_op_K, ALU_op_PL, Arith_op, Arith_op_K, Arith_op_PL, Comparator_op, Comparator_op_K,
       Comparator_op_PL, Forward_A, Forward_B, Logical_op, Logical_op_K, Logical_op_PL, MUX_ALU, MUX_ALU_K,
       MUX_ALU_PL, MUX_S2_or_Imm16, MUX_S2_or_Imm16_K, MUX_S2_or_Imm16_PL, Shifter_op, Shifter_op_K,
       Shifter_op_PL;
  wire [4:0] multiplexer_2_out, multiplexer_7_out, RD, RD_PL, RD_PL_1, RD_PL_2, S1, S2;
  wire [5:0] Opcode, Opcode_PL;
  wire [10:0] ImmU_F, ImmU_F_PL;
  wire [15:0] Imm16, Imm16_PL;
  wire [19:0] Branch_PL, Branch_PL_1;
  wire [23:23] multiplexer_5_out, undriven;
  wire [31:0] ALU_res, bit_extender_2_out, BusD, BusS2, BusS2_PL, DM, Imm16_E, main_3_out_2, main_4_p7,
       main_8_out_9, main_8_out_10, main_11_out_13, main_12_out_16, main_12_out_17, main_13_p4,
       multiplexer_1_out, multiplexer_6_out, multiplexer_10_out, PC_1, PC_1_PL, PC_1_PL_1, PC_1_PL_2, RS1,
       RS1_PL, SET, SW;

  PC_main main_1 (
    .in_2(ImmU_F_PL), .in_5(RD_PL), .in_1(RS1_PL), .out_10(PC_1), .in_4(CLK), .in_3(Imm16_PL),
    .out_11(out_33), .in_6(Branch), .in_7(JALR), .in_8(Stall), .in_9(Branch_PL_1));
  PC_Control_Unit_main main_2 (
    .BEQ(BEQ_BNE), .in_2(Opcode_PL), .BNQ(BEQ_BNE), .BLT(BLT), .BGE(BQE), .BLTU(BLTU), .BGEU(BGEU),
    .JALR(JALR), .Branch(Branch), .kill1(Kill1), .Kill2(Kill2));
  Inst_memory_main main_3 (.in_1(out_33), .out_2(main_3_out_2));
  Multiplexer #(.width(32), .enable("false")) multiplexer_1 (
    .in0(main_3_out_2), .in1({32{1'b0}}), .out(multiplexer_1_out), .sel(Kill1));
  // IF_ID_main main_4: pin names not known; wires that end beside it: out_33, multiplexer_1_out, PC_1, CLK, Stall, Branch_PL, main_4_p7, PC_1_PL
  Instruction_coulmn_main main_5 (
    .in_1(main_4_p7), .out_2(Opcode), .out_3(RD), .out_7(Imm16), .out_4(S1), .out_5(S2), .out_6(ImmU_F));
  // Main_Control_Unit_main main_6: pin names not known; wires that end beside it: Opcode, Mem_Read, MUX_RD_1, MemWrite, MUX_RD_2, MUX_ALU, MUX_RS1_RD, RegWrite, MUX_Extender, MUX_S2_or_Imm16, MUX_SA_RS2, ALU_ctrl
  Multiplexer #(.width(5), .enable("false")) multiplexer_2 (
    .in0(S2), .in1(RD), .out(multiplexer_2_out), .sel(MUX_RS1_RD));
  ALU_control_unit_main main_7 (
    .in_1(ImmU_F), .in_2(Opcode), .Signal_of_add(Signal_OF_ADD), .Signal_of_sub(Signal_OF_SUB),
    .Arith_op(Arith_op), .Logical_op(Logical_op), .Comprator_op(Comparator_op), .Shifter_op(Shifter_op),
    .Alu_op(ALU_op), .in_3(ALU_ctrl));
  RF_main main_8 (
    .RW(RD_PL_2), .RA(S1), .RB(multiplexer_2_out), .in_6(CLK), .out_9(main_8_out_9), .out_10(main_8_out_10),
    .in_4(BusD), .in_5(RegWrite_PL_2), .out_11(out_1), .out_12(out_2), .out_13(out_3), .out_14(out_4),
    .out_15(out_5), .out_16(out_6), .out_17(out_7), .out_18(out_8), .out_27(out_17), .out_28(out_18),
    .out_29(out_19), .out_30(out_20), .out_31(out_21), .out_32(out_22), .out_33(out_23), .out_34(out_24),
    .out_19(out_9), .out_20(out_10), .out_21(out_11), .out_22(out_12), .out_23(out_13), .out_24(out_14),
    .out_25(out_15), .out_26(out_16), .out_35(out_25), .out_36(out_26), .out_37(out_27), .out_38(out_28),
    .out_39(out_29), .out_40(out_30), .out_41(out_31), .out_42(out_32), .in_7(S2));  // open: out_43, out_44, in_8
  Multiplexer #(.select(2), .width(32), .enable("false")) multiplexer_3 (
    .in0(main_8_out_9), .in1(ALU_res), .in2(DM), .in3(BusD), .out(RS1), .sel(Forward_A));
  Multiplexer #(.select(2), .width(32), .enable("false")) multiplexer_4 (
    .in0(main_8_out_10), .in1(ALU_res), .in2(DM), .in3(BusD), .out(BusS2), .sel(Forward_B));
  Multiplexer #(.width(24), .enable("false")) multiplexer_5 (
    .in0({undriven[23], MUX_ALU, MUX_Extender, MUX_S2_or_Imm16, ALU_op, Shifter_op, Comparator_op, Logical_op, Arith_op, MUX_RD_1, MemWrite, Mem_Read, MUX_RD_2, MUX_SA_RS2, RegWrite, Signal_OF_SUB, Signal_OF_ADD}),
    .in1({24{1'b0}}),
    .out({multiplexer_5_out[23], MUX_ALU_K, MUX_Extender_K, MUX_S2_or_Imm16_K, ALU_op_K, Shifter_op_K, Comparator_op_K, Logical_op_K, Arith_op_K, MUX_RD_1_K, MemWrite_K, Mem_Read_K, MUX_RD_2_K, MUX_SA_RS2_K, RegWrite_K, Signal_OF_SUB_K, Signal_OF_ADD_K}),
    .sel(or_1_out));
  or or_1 (or_1_out, Stall, Kill2);
  Forward_stall_Control_main main_9 (
    .out_12(Forward_A), .in_1(S1), .in_2(S2), .in_4(RD_PL), .in_5(RD_PL_1), .in_6(RD_PL_2),
    .in_7(RegWrite_PL), .in_8(RegWrite_PL_1), .in_9(RegWrite_PL_2), .in_10(Mem_Read_PL), .out_13(Forward_B),
    .out_14(Stall), .in_3(RD));  // open: in_11
  ID_EX_main main_10 (
    .in_1(RS1), .in_2(BusS2), .in_3(RD), .in_5(ImmU_F), .in_6(Branch_PL), .in_7(PC_1_PL), .out_27(RS1_PL),
    .out_28(BusS2_PL), .out_29(RD_PL), .out_31(ImmU_F_PL), .out_32(Branch_PL_1), .out_33(PC_1_PL_1),
    .CLK(CLK), .Mux_RD_1(MUX_RD_1_K), .Arith_op(Arith_op_K), .Signal_of_add(Signal_OF_ADD_K),
    .Signal_of_Sub(Signal_OF_SUB_K), .Reg_Write(RegWrite_K), .Logical_op(Logical_op_K),
    .Mux_SA_RS2(MUX_SA_RS2_K), .Mux_RD2(MUX_RD_2_K), .MEM_Read(Mem_Read_K), .MEM_Write(MemWrite_K),
    .Comprator_op(Comparator_op_K), .Shifter_op(Shifter_op_K), .ALU_op(ALU_op_K),
    .Signal_of_add_2(Signal_OF_ADD_PL), .Signal_of_Sub_2(Signal_OF_SUB_PL), .Reg_Write_2(RegWrite_PL),
    .Mux_SA_RS2_2(MUX_SA_RS2_PL), .Mux_RD2_2(MUX_RD_2_PL), .MEM_Read_2(Mem_Read_PL),
    .MEM_Write_2(MemWrite_PL), .Mux_RD_1_2(MUX_RD_1_PL), .Arith_op_2(Arith_op_PL),
    .Logical_op_2(Logical_op_PL), .Comprator_op_2(Comparator_op_PL), .Shifter_op_2(Shifter_op_PL),
    .ALU_op_2(ALU_op_PL), .in_25(MUX_S2_or_Imm16_K), .MUX_S2_or_Imm16(MUX_S2_or_Imm16_PL), .in_4(Imm16),
    .out_30(Imm16_PL), .in_8(Opcode), .out_34(Opcode_PL), .MUX_Extender(MUX_Extender_K),
    .MUX_Extender_2(MUX_Extender_PL), .MUX_ALU(MUX_ALU_K), .MUX_ALU_2(MUX_ALU_PL));  // open: JALR, JALR_2
  // Probe on out_1
  // Probe on out_12
  // Probe on out_23
  Multiplexer #(.select(2), .width(32), .enable("false")) multiplexer_6 (
    .in0(BusS2_PL), .in1(Imm16_E), .in2(SW), .out(multiplexer_6_out), .sel(MUX_S2_or_Imm16_PL));  // open: in3
  // Probe on out_2
  // Probe on out_13
  // Probe on out_24
  Multiplexer #(.width(5), .enable("false")) multiplexer_7 (
    .in0(Imm16_PL[4:0]), .in1(BusS2_PL[4:0]), .out(multiplexer_7_out), .sel(MUX_SA_RS2_PL));
  // Probe on out_3
  // Probe on out_14
  // Probe on out_25
  assign SET = {{16{Imm16_PL[15]}}, Imm16_PL};  // Bit_Extender bit_extender_1
  assign bit_extender_2_out = {{16{1'b0}}, Imm16_PL};  // Bit_Extender bit_extender_2
  // Probe on out_4
  // Probe on out_15
  // Probe on out_26
  // Probe on main_11_out_12
  // Probe on out_5
  // Probe on out_16
  // Probe on out_27
  ALU_main main_11 (
    .out_11(BLT), .out_14(BLTU), .out_16(BQE), .out_17(BGEU), .in_1(RS1_PL), .in_2(multiplexer_6_out),
    .in_3(multiplexer_7_out), .in_4(Signal_OF_ADD_PL), .in_5(Signal_OF_SUB_PL), .out_12(main_11_out_12),
    .in_6(Arith_op_PL), .in_7(Logical_op_PL), .in_8(Shifter_op_PL), .in_9(Comparator_op_PL),
    .in_10(ALU_op_PL), .out_13(main_11_out_13), .out_15(BEQ_BNE));
  Multiplexer #(.width(32), .enable("false")) multiplexer_8 (
    .in0(SET), .in1(bit_extender_2_out), .out(Imm16_E), .sel(MUX_Extender_PL));
  // Probe on out_6
  // Probe on out_17
  // Probe on out_28
  Multiplexer #(.select(2), .width(32), .enable("false")) multiplexer_9 (
    .in0(main_11_out_13), .in1(SET), .in2({BusS2_PL[15:0], Imm16_PL}), .out(ALU_res), .sel(MUX_ALU_PL));  // open: in3
  // Probe on out_7
  // Probe on out_18
  // Probe on out_29
  assign SW = {{16{ImmU_F_PL[10]}}, {ImmU_F_PL, RD_PL}};  // Bit_Extender bit_extender_3
  // Probe on out_8
  // Probe on out_19
  // Probe on out_30
  // Probe on out_9
  // Probe on out_20
  // Probe on out_31
  EX_MEM_main main_12 (
    .in_2(ALU_res), .in_3(BusS2_PL), .in_4(PC_1_PL_1), .in_1(CLK), .out_16(main_12_out_16),
    .out_17(main_12_out_17), .out_18(PC_1_PL_2), .in_5(RD_PL), .out_19(RD_PL_1), .in_6(Mem_Read_PL),
    .in_7(MemWrite_PL), .in_8(MUX_RD_1_PL), .in_9(MUX_RD_2_PL), .out_11(Mem_Read_PL_1),
    .out_12(MemWrite_PL_1), .out_13(MUX_RD_1_PL_1), .out_14(MUX_RD_2_PL_1), .in_10(RegWrite_PL),
    .out_15(RegWrite_PL_1));
  // Probe on out_10
  // Probe on out_21
  // Probe on out_32
  // Probe on out_11
  // Probe on out_22
  Clock clock_1 (.out(CLK));
  // data_memorypl_main main_13: pin names not known; wires that end beside it: Mem_Read_PL_1, CLK, MemWrite_PL_1, main_13_p4
  Multiplexer #(.width(32), .enable("false")) multiplexer_10 (
    .in0(main_12_out_16), .in1(main_13_p4), .out(multiplexer_10_out), .sel(MUX_RD_1_PL_1));
  Multiplexer #(.width(32), .enable("false")) multiplexer_11 (
    .in0(multiplexer_10_out), .in1(PC_1_PL_2), .out(DM), .sel(MUX_RD_2_PL_1));
  // Probe on BusD
  MEM_WB_main main_14 (
    .in_1(DM), .in_3(RD_PL_1), .out_5(BusD), .out_6(RD_PL_2), .in_2(CLK), .in_4(RegWrite_PL_1),
    .out_7(RegWrite_PL_2));

  // Other names for the same wires on the sheet: SSET[31:0] = {BusS2_PL[15:0], Imm16_PL}; PC[19:0] = out_33;
  //   R0[31:0] = out_1; R1[31:0] = out_2; R2[31:0] = out_3; R3[31:0] = out_4; R4[31:0] = out_5; R5[31:0] = out_6;
  //   R6[31:0] = out_7; R7[31:0] = out_8; R8[31:0] = out_9; R9[31:0] = out_10; R10[31:0] = out_11; R11[31:0] = out_12;
  //   R12[31:0] = out_13; R13[31:0] = out_14; R14[31:0] = out_15; R15[31:0] = out_16; R16[31:0] = out_17;
  //   R17[31:0] = out_18; R18[31:0] = out_19; R19[31:0] = out_20; R20[31:0] = out_21; R21[31:0] = out_22;
  //   R22[31:0] = out_23; R23[31:0] = out_24; R24[31:0] = out_25; R25[31:0] = out_26; R26[31:0] = out_27;
  //   R27[31:0] = out_28; R28[31:0] = out_29; R29[31:0] = out_30; R30[31:0] = out_31; R31[31:0] = out_32;
  //   SA[4:0] = Imm16_PL[4:0]
endmodule
