// Logisim project EX_MEM.circ as structural Verilog: 1 circuit, main circuit main
module main (
  input  in_1,
  input  [31:0] in_2,
  input  [31:0] in_3,
  input  [31:0] in_4,
  input  [4:0] in_5,
  input  in_6,
  input  in_7,
  input  in_8,
  input  in_9,
  input  in_10,
  output out_11,
  output out_12,
  output out_13,
  output out_14,
  output out_15,
  output [31:0] out_16,
  output [31:0] out_17,
  output [31:0] out_18,
  output [4:0] out_19
);

  Register #(.width(32)) register_1 (.D(in_2), .en(1'b1), .clk(in_1), .Q(out_16));  // open: clr
  Register #(.width(32)) register_2 (.D(in_3), .en(1'b1), .clk(in_1), .Q(out_17));  // open: clr
  Register #(.width(32)) register_3 (.D(in_4), .en(1'b1), .clk(in_1), .Q(out_18));  // open: clr
  Register #(.width(5)) register_4 (.D(in_5), .en(1'b1), .clk(in_1), .Q(out_19));  // open: clr
  Register #(.width(5)) register_5 (
    .D({in_10, in_9, in_8, in_7, in_6}), .en(1'b1), .clk(in_1), .Q({out_15, out_14, out_13, out_12, out_11}));  // open: clr

  // Other names for the same wires on the sheet: MemRead = out_11; MemWrite = out_12; MUX_RD_1 = out_13;
  //   MUX_RD_2 = out_14; RegWrite = out_15; ALU_res[31:0] = out_16; CLK = in_1; PC_1[31:0] = out_18; RD[4:0] = out_19;
  //   RS2[31:0] = out_17
endmodule
