// Logisim project Forward_stall_Control.circ as structural Verilog: 1 circuit, main circuit main
module main (
  input  [4:0] in_1,
  input  [4:0] in_2,
  input  [4:0] in_3,
  input  [4:0] in_4,
  input  [4:0] in_5,
  input  [4:0] in_6,
  input  in_7,
  input  in_8,
  input  in_9,
  input  in_10,
  input  in_11,
  output [1:0] out_12,
  output [1:0] out_13,
  output out_14
);

  wire and_4_out, and_5_out, and_10_out, and_11_out, comparator_3_eq, comparator_7_eq, comparator_11_eq,
       Forward0_1, Forward0_2, Forward1_1, Forward1_2, Forward2_1, Forward2_2, Forward3_1, Forward3_2,
       ForwardA_EQ_1, ForwardB_EQ_1, not_4_out, not_5_out, not_7_out, or_1_out, RD_EQ_RD2, RD_EQ_RD3,
       RD_EQ_RD4, RD_NEQZ, RS1_EQ_RD2, RS1_EQ_RD3, RS1_EQ_RD4, RS1_NEQZ, RS2_EQ_RD2, RS2_EQ_RD3, RS2_EQ_RD4,
       RS2_NEQZ;

  Comparator #(.width(2), .mode("unsigned")) comparator_1 (.a(out_12), .b(2'b01), .eq(ForwardA_EQ_1));  // open: gt, lt
  Comparator #(.width(2), .mode("unsigned")) comparator_2 (.a(out_13), .b(2'b01), .eq(ForwardB_EQ_1));  // open: gt, lt
  Comparator #(.width(5), .mode("unsigned")) comparator_3 (
    .a(in_1), .b({5{1'b0}}), .eq(comparator_3_eq));  // open: gt, lt
  Comparator #(.width(5), .mode("unsigned")) comparator_4 (.a(in_1), .b(in_4), .eq(RS1_EQ_RD2));  // open: gt, lt
  Comparator #(.width(5), .mode("unsigned")) comparator_5 (.a(in_1), .b(in_5), .eq(RS1_EQ_RD3));  // open: gt, lt
  Comparator #(.width(5), .mode("unsigned")) comparator_6 (.a(in_1), .b(in_6), .eq(RS1_EQ_RD4));  // open: gt, lt
  not not_1 (RS1_NEQZ, comparator_3_eq);
  Comparator #(.width(5), .mode("unsigned")) comparator_7 (
    .a(in_2), .b({5{1'b0}}), .eq(comparator_7_eq));  // open: gt, lt
  not not_2 (RS2_NEQZ, comparator_7_eq);
  Comparator #(.width(5), .mode("unsigned")) comparator_8 (.a(in_2), .b(in_4), .eq(RS2_EQ_RD2));  // open: gt, lt
  Comparator #(.width(5), .mode("unsigned")) comparator_9 (.a(in_2), .b(in_5), .eq(RS2_EQ_RD3));  // open: gt, lt
  Comparator #(.width(5), .mode("unsigned")) comparator_10 (.a(in_2), .b(in_6), .eq(RS2_EQ_RD4));  // open: gt, lt
  not not_3 (RD_NEQZ, comparator_11_eq);
  Comparator #(.width(5), .mode("unsigned")) comparator_11 (
    .a(in_3), .b({5{1'b0}}), .eq(comparator_11_eq));  // open: gt, lt
  Comparator #(.width(5), .mode("unsigned")) comparator_12 (.a(in_3), .b(in_4), .eq(RD_EQ_RD2));  // open: gt, lt
  Comparator #(.width(5), .mode("unsigned")) comparator_13 (.a(in_3), .b(in_5), .eq(RD_EQ_RD3));  // open: gt, lt
  Comparator #(.width(5), .mode("unsigned")) comparator_14 (.a(in_3), .b(in_6), .eq(RD_EQ_RD4));  // open: gt, lt
  and and_1 (Forward1_1, RS1_NEQZ, RS1_EQ_RD2, in_7);
  and and_2 (Forward2_1, RS1_NEQZ, RS1_EQ_RD3, in_8);
  and and_3 (Forward3_1, RS1_NEQZ, RS1_EQ_RD4, in_9);
  nor nor_1 (Forward0_1, Forward1_1, Forward2_1, Forward3_1);
  or or_1 (or_1_out, ForwardA_EQ_1, ForwardB_EQ_1);
  assign out_12 = Forward1_1 ? 2'b01 : 2'bz;  // Controlled_Buffer controlled_buffer_1
  assign out_12 = and_4_out ? 2'b10 : 2'bz;  // Controlled_Buffer controlled_buffer_2
  and and_4 (and_4_out, ~Forward1_1, Forward2_1);  // AND_Gate
  assign out_12 = and_5_out ? 2'b11 : 2'bz;  // Controlled_Buffer controlled_buffer_3
  and and_5 (and_5_out, ~Forward1_1, Forward3_1, ~Forward2_1);  // AND_Gate
  assign out_12 = Forward0_1 ? 2'b00 : 2'bz;  // Controlled_Buffer controlled_buffer_4
  not not_4 (not_4_out, in_11);
  not not_5 (not_5_out, in_11);
  not not_6 (not_5_out, in_11);
  not not_7 (not_7_out, in_11);
  and and_6 (Forward1_2, RS2_NEQZ, RS2_EQ_RD2, not_4_out, in_7);
  and and_7 (Forward2_2, RS2_NEQZ, RS2_EQ_RD3, not_5_out, in_8);
  and and_8 (Forward3_2, RS2_NEQZ, RS2_EQ_RD4, not_7_out, in_9);
  nor nor_2 (Forward0_2, Forward1_2, Forward2_2, Forward3_2);
  and and_9 (out_14, or_1_out, in_10);
  assign out_13 = Forward1_2 ? 2'b01 : 2'bz;  // Controlled_Buffer controlled_buffer_5
  assign out_13 = and_10_out ? 2'b10 : 2'bz;  // Controlled_Buffer controlled_buffer_6
  and and_10 (and_10_out, ~Forward1_2, Forward2_2);  // AND_Gate
  assign out_13 = and_11_out ? 2'b11 : 2'bz;  // Controlled_Buffer controlled_buffer_7
  and and_11 (and_11_out, ~Forward1_2, Forward3_2, ~Forward2_2);  // AND_Gate
  assign out_13 = Forward0_2 ? 2'b00 : 2'bz;  // Controlled_Buffer controlled_buffer_8

  // Other names for the same wires on the sheet: EX_MEM_Read = in_10; EX_RegWrite = in_7; ForwardA[1:0] = out_12;
  //   ForwardB[1:0] = out_13; iSignal = in_11; MEM_RegWrite = in_8; RD[4:0] = in_3; RD2[4:0] = in_4; RD3[4:0] = in_5;
  //   RD4[4:0] = in_6; RS1[4:0] = in_1; RS2[4:0] = in_2; Stall = out_14; WB_RegWrite = in_9
endmodule
