// Logisim project ID_EX.circ as structural Verilog: 1 circuit, main circuit main
module main (
  input  [31:0] in_1,
  input  [31:0] in_2,
  input  [4:0] in_3,
  input  [15:0] in_4,
  input  [10:0] in_5,
  input  [19:0] in_6,
  input  [31:0] in_7,
  input  [5:0] in_8,
  input  Signal_of_add,
  input  Signal_of_Sub,
  input  Reg_Write,
  input  Mux_SA_RS2,
  input  Mux_RD2,
  input  MEM_Read,
  input  MEM_Write,
  input  MUX_Extender,
  input  JALR,
  input  Mux_RD_1,
  input  [1:0] Arith_op,
  input  [1:0] Logical_op,
  input  CLK,
  input  [1:0] Comprator_op,
  input  [1:0] Shifter_op,
  input  [1:0] ALU_op,
  input  [1:0] in_25,
  input  [1:0] MUX_ALU,
  output [31:0] out_27,
  output [31:0] out_28,
  output [4:0] out_29,
  output [15:0] out_30,
  output [10:0] out_31,
  output [19:0] out_32,
  output [31:0] out_33,
  output [5:0] out_34,
  output Signal_of_add_2,
  output Signal_of_Sub_2,
  output Reg_Write_2,
  output Mux_SA_RS2_2,
  output Mux_RD2_2,
  output MEM_Read_2,
  output MEM_Write_2,
  output MUX_Extender_2,
  output JALR_2,
  output Mux_RD_1_2,
  output [1:0] Arith_op_2,
  output [1:0] Logical_op_2,
  output [1:0] Comprator_op_2,
  output [1:0] Shifter_op_2,
  output [1:0] ALU_op_2,
  output [1:0] MUX_S2_or_Imm16,
  output [1:0] MUX_ALU_2
);

  Register #(.width(32)) BusS1 (.D(in_1), .en(1'b1), .clk(CLK), .Q(out_27));  // open: clr
  Register #(.width(32)) BusS2 (.D(in_2), .en(1'b1), .clk(CLK), .Q(out_28));  // open: clr
  Register #(.width(5)) RD (.D(in_3), .en(1'b1), .clk(CLK), .Q(out_29));  // open: clr
  Register #(.width(16)) register_1 (.D(in_4), .en(1'b1), .clk(CLK), .Q(out_30));  // open: clr
  Register #(.width(11)) ImmU (.D(in_5), .en(1'b1), .clk(CLK), .Q(out_31));  // open: clr
  Register #(.width(20)) Branch_address (.D(in_6), .en(1'b1), .clk(CLK), .Q(out_32));  // open: clr
  Register #(.width(32)) PC_1 (.D(in_7), .en(1'b1), .clk(CLK), .Q(out_33));  // open: clr
  Register #(.width(6)) register_2 (.D(in_8), .en(1'b1), .clk(CLK), .Q(out_34));  // open: clr
  Register #(.width(9)) Signals_1bit (
    .D({JALR, MUX_Extender, MEM_Write, MEM_Read, Mux_RD2, Mux_SA_RS2, Reg_Write, Signal_of_Sub, Signal_of_add}),
    .en(1'b1), .clk(CLK),
    .Q({JALR_2, MUX_Extender_2, MEM_Write_2, MEM_Read_2, Mux_RD2_2, Mux_SA_RS2_2, Reg_Write_2, Signal_of_Sub_2, Signal_of_add_2}));  // open: clr
  Register #(.width(15)) Signals_2bit (
    .D({MUX_ALU, in_25, ALU_op, Shifter_op, Comprator_op, Logical_op, Arith_op, Mux_RD_1}), .en(1'b1),
    .clk(CLK),
    .Q({MUX_ALU_2, MUX_S2_or_Imm16, ALU_op_2, Shifter_op_2, Comprator_op_2, Logical_op_2, Arith_op_2, Mux_RD_1_2}));  // open: clr

  // Notes on the sheet:
  //   MUX_S2_or_Imm16
  //   Imm16
  //   Opcode
endmodule
