// Logisim project IF_ID.circ as structural Verilog: 1 circuit, main circuit main
module main (
  input  [31:0] in_1,
  input  [31:0] in_2,
  input  [19:0] in_3,
  input  in_4,
  input  in_5,
  output [31:0] out_6,
  output [19:0] out_7,
  output [31:0] out_8
);

  wire multiplexer_1_out;

  Multiplexer #(.enable("false")) multiplexer_1 (.in0(1'b1), .in1(1'b0), .out(multiplexer_1_out), .sel(in_4));
  Register #(.width(20)) PC_Branch (.D(in_3), .en(1'b1), .clk(in_5), .Q(out_7));  // open: clr
  Register #(.width(32)) Instruction (.D(in_2), .en(multiplexer_1_out), .clk(in_5), .Q(out_8));  // open: clr
  Register #(.width(32)) PC_Register (.D(in_1), .en(1'b1), .clk(in_5), .Q(out_6));  // open: clr

  // Other names for the same wires on the sheet: Branch[19:0] = out_7; Instruction[31:0] = in_2;
  //   Next_pc[31:0] = out_6; pc_1[31:0] = in_1; PC_Branch[19:0] = in_3; Sub_instruction[31:0] = out_8
endmodule
