// Logisim project Instruction_coulmn.circ as structural Verilog: 1 circuit, main circuit main
module main (
  input  [31:0] in_1,
  output [5:0] out_2,
  output [4:0] out_3,
  output [4:0] out_4,
  output [4:0] out_5,
  output [10:0] out_6,
  output [15:0] out_7
);


  assign out_2 = in_1[5:0];
  assign out_3 = in_1[10:6];
  assign out_4 = in_1[15:11];
  assign out_5 = in_1[20:16];
  assign out_6 = in_1[31:21];
  assign out_7 = in_1[31:16];

  // Other names for the same wires on the sheet: op[5:0] = in_1[5:0]; sub_instruction[31:0] = in_1;
  //   d_ImmL[4:0] = in_1[10:6]; S1[4:0] = in_1[15:11]; Imm16[15:0] = in_1[31:16]; S2[4:0] = in_1[20:16];
  //   F_ImmU[10:0] = in_1[31:21]
endmodule
