// Logisim project Main.circ as structural Verilog: 1 circuit, main circuit main
module main (
  input  [5:0] in_1,
  output [1:0] out_2,
  output MUX_RD_1
);

  wire and_1_out, and_2_out, and_3_out, and_4_out, and_5_out, and_6_out, and_7_out, not_1_out, not_2_out,
       not_3_out, not_4_out, not_5_out;

  not not_1 (not_1_out, in_1[4]);
  not not_2 (not_2_out, in_1[5]);
  not not_3 (not_3_out, in_1[3]);
  not not_4 (not_4_out, in_1[4]);
  not not_5 (not_5_out, in_1[3]);
  and and_1 (and_1_out, not_1_out, in_1[3], in_1[2], in_1[1]);
  and and_2 (and_2_out, not_2_out, in_1[4], not_3_out, in_1[1]);
  and and_3 (and_3_out, in_1[5], in_1[3], in_1[2], in_1[1]);
  and and_4 (and_4_out, not_4_out, in_1[3], in_1[2], in_1[0]);
  and and_5 (and_5_out, in_1[5], in_1[3], in_1[2], in_1[0]);
  and and_6 (and_6_out, in_1[4], not_5_out);
  and and_7 (and_7_out, in_1[5], in_1[4]);
  or or_1 (out_2[1], and_1_out, and_2_out, and_3_out);
  or or_2 (out_2[0], and_4_out, and_5_out);
  or or_3 (MUX_RD_1, and_6_out, and_7_out);
endmodule
