// Logisim project Main_Control_Unit.circ as structural Verilog: 3 circuits, main circuit main
module main (
  input  [5:0] in_1,
  output RegWrite,
  output MUX_Extender,
  output [1:0] out_4,
  output out_5,
  output [1:0] MUX_S2_or_Imm16,
  output out_7,
  output out_8,
  output MUX_SA_RS2,
  output MUX_RD_2,
  output MemRead,
  output MemWrite,
  output ALUctrl
);

  wire and_2_out, and_3_out, and_4_out, and_5_out, and_6_out, and_8_out, and_9_out, and_10_out, and_11_out,
       and_12_out, not_1_out, not_2_out, not_3_out, not_4_out, not_5_out, not_6_out, not_7_out, not_8_out,
       not_9_out, not_10_out, not_11_out, not_12_out, not_13_out, not_14_out, not_15_out, not_16_out,
       not_17_out, not_18_out, not_19_out, not_20_out, not_21_out, not_22_out, not_23_out, or_1_out, or_2_out;

  and and_1 (out_7, in_1[1], in_1[2], in_1[3]);
  not not_1 (not_1_out, in_1[2]);
  not not_2 (not_2_out, in_1[1]);
  not not_3 (not_3_out, in_1[0]);
  not not_4 (not_4_out, in_1[2]);
  not not_5 (not_5_out, in_1[2]);
  not not_6 (not_6_out, in_1[1]);
  not not_7 (not_7_out, in_1[0]);
  not not_8 (not_8_out, in_1[3]);
  not not_9 (not_9_out, in_1[2]);
  not not_10 (not_10_out, in_1[1]);
  not not_11 (not_11_out, in_1[2]);
  not not_12 (not_12_out, in_1[1]);
  not not_13 (not_13_out, in_1[0]);
  not not_14 (not_14_out, in_1[2]);
  not not_15 (not_15_out, in_1[1]);
  not not_16 (not_16_out, in_1[0]);
  not not_17 (not_17_out, in_1[2]);
  not not_18 (not_18_out, in_1[1]);
  not not_19 (not_19_out, in_1[0]);
  not not_20 (not_20_out, in_1[2]);
  not not_21 (not_21_out, in_1[1]);
  not not_22 (not_22_out, in_1[4]);
  and and_2 (and_2_out, not_1_out, not_2_out, not_3_out);
  and and_3 (and_3_out, not_4_out, in_1[0]);
  and and_4 (and_4_out, not_5_out, in_1[1]);
  and and_5 (and_5_out, in_1[1], in_1[0]);
  and and_6 (and_6_out, in_1[2], not_6_out, not_7_out);
  and and_7 (MUX_S2_or_Imm16[1], not_8_out, not_9_out, not_10_out, in_1[0]);
  not not_23 (not_23_out, in_1[4]);
  and and_8 (and_8_out, not_23_out, in_1[2]);
  and and_9 (and_9_out, in_1[4], not_11_out, not_12_out, not_13_out);
  and and_10 (and_10_out, in_1[3], in_1[2], in_1[0]);
  or or_1 (or_1_out, and_10_out, and_11_out);
  and and_11 (and_11_out, in_1[3], in_1[2], in_1[1]);
  and and_12 (and_12_out, in_1[3], in_1[2], in_1[1]);
  or or_2 (or_2_out, and_12_out, in_1[4]);
  and and_13 (MUX_SA_RS2, not_14_out, not_15_out, not_16_out);
  and and_14 (MUX_RD_2, in_1[3], in_1[2], in_1[1], in_1[0]);
  and and_15 (MemRead, in_1[4], not_17_out, not_18_out, not_19_out);
  and and_16 (MemWrite, in_1[4], not_20_out, not_21_out, in_1[0]);
  or or_3 (ALUctrl, in_1[0], in_1[1], in_1[2], in_1[3], in_1[4]);
  or or_4 (RegWrite, not_22_out, and_2_out);
  or or_5 (MUX_Extender, and_3_out, and_4_out, and_5_out, and_6_out);
  or or_6 (MUX_S2_or_Imm16[0], and_8_out, in_1[3], and_9_out);
  Main_main main_1 (.in_1(in_1), .out_2(out_4), .MUX_RD_1(out_5));
  Isignal isignal_1 (.op(in_1), .I_type_signal(out_8));

  // Other names for the same wires on the sheet: OP[5:0] = in_1
endmodule

module Itypesignal (
  input  [5:0] op,
  output I_type_signal
);

  wire and_1_out, and_2_out, and_3_out, and_4_out, and_5_out, not_1_out, not_2_out, not_3_out, not_4_out,
       not_5_out, not_6_out;

  not not_1 (not_1_out, op[5]);
  not not_2 (not_2_out, op[4]);
  not not_3 (not_3_out, op[3]);
  not not_4 (not_4_out, op[2]);
  not not_5 (not_5_out, op[1]);
  not not_6 (not_6_out, op[0]);
  and and_1 (and_1_out, not_1_out, not_2_out, op[0]);
  and and_2 (and_2_out, not_1_out, not_2_out, op[1]);
  and and_3 (and_3_out, not_1_out, not_2_out, op[2]);
  and and_4 (and_4_out, not_1_out, not_2_out, op[3]);
  and and_5 (and_5_out, not_1_out, op[4], not_3_out, not_4_out, not_5_out, not_6_out);
  or or_1 (I_type_signal, and_1_out, and_2_out, and_3_out, and_4_out, and_5_out);
endmodule

module Isignal (
  input  [5:0] op,
  output I_type_signal
);

  wire and_1_out, and_2_out, and_3_out, and_4_out, and_5_out, not_1_out, not_2_out, not_3_out, not_4_out,
       not_5_out, not_6_out;

  not not_1 (not_1_out, op[5]);
  not not_2 (not_2_out, op[4]);
  not not_3 (not_3_out, op[3]);
  not not_4 (not_4_out, op[2]);
  not not_5 (not_5_out, op[1]);
  not not_6 (not_6_out, op[0]);
  and and_1 (and_1_out, not_1_out, not_2_out, op[0]);
  and and_2 (and_2_out, not_1_out, not_2_out, op[1]);
  and and_3 (and_3_out, not_1_out, not_2_out, op[2]);
  and and_4 (and_4_out, not_1_out, not_2_out, op[3]);
  and and_5 (and_5_out, not_1_out, op[4], not_3_out, not_4_out, not_5_out, not_6_out);
  or or_1 (I_type_signal, and_1_out, and_2_out, and_3_out, and_4_out, and_5_out);
endmodule
