// Logisim project PC_Control_Unit.circ as structural Verilog: 1 circuit, main circuit main
module main (
  input  BEQ,
  input  [5:0] in_2,
  input  BNQ,
  input  BLT,
  input  BGE,
  input  BLTU,
  input  BGEU,
  output JALR,
  output Branch,
  output kill1,
  output Kill2
);

  wire and_1_out, and_2_out, and_3_out, and_4_out, and_5_out, and_6_out, and_7_out, and_8_out, and_9_out,
       and_10_out, and_11_out, and_12_out, and_13_out, not_1_out, not_2_out, not_3_out, not_4_out, not_5_out,
       not_6_out, not_7_out, not_8_out;

  and and_1 (and_1_out, in_2[3], in_2[2], in_2[1], in_2[0]);
  not not_1 (not_1_out, in_2[2]);
  not not_2 (not_2_out, in_2[0]);
  not not_3 (not_3_out, in_2[2]);
  not not_4 (not_4_out, in_2[1]);
  not not_5 (not_5_out, in_2[0]);
  not not_6 (not_6_out, in_2[1]);
  not not_7 (not_7_out, in_2[0]);
  and and_2 (and_2_out, in_2[4], in_2[2], in_2[1], in_2[0]);
  and and_3 (and_3_out, in_2[4], not_1_out, in_2[1], not_2_out);
  and and_4 (and_4_out, in_2[4], not_3_out, in_2[1], in_2[0]);
  and and_5 (and_5_out, in_2[4], in_2[2], not_4_out, not_5_out);
  and and_6 (and_6_out, in_2[4], in_2[2], not_6_out, in_2[0]);
  and and_7 (and_7_out, in_2[4], in_2[2], in_2[1], not_7_out);
  and and_8 (and_8_out, and_3_out, BEQ);
  and and_9 (and_9_out, and_4_out, ~BNQ);  // AND_Gate
  and and_10 (and_10_out, and_5_out, BLT);
  and and_11 (and_11_out, and_6_out, BGE);
  and and_12 (and_12_out, and_7_out, BLTU);
  and and_13 (and_13_out, and_2_out, BGEU);
  or or_1 (Branch, and_8_out, and_9_out, and_10_out, and_11_out, and_12_out, and_13_out);
  not not_8 (not_8_out, Branch);
  and and_14 (JALR, and_1_out, not_8_out);
  or or_2 (kill1, JALR, Branch);

  assign Kill2 = Branch;
endmodule
