// Logisim project Arith_unit.circ as structural Verilog: 1 circuit, main circuit main
module main (
  input  in_1,
  input  [31:0] in_2,
  input  [31:0] in_3,
  input  [1:0] in_4,
  input  in_5,
  output [31:0] out_6,
  output out_7
);

  wire A_Larger, and_1_out, and_2_out, and_3_out, and_4_out, B_Larger, N_IN1, N_IN2, NANDOUT, NSUBOUT,
       or_2_out, or_3_out, Overflow_AND, Overflow_SUB, P_IN1, P_IN2, PANDOUT, PSUBOUT;
  wire [31:0] ANDOUT, MULOUT, SUBOUT;

  or or_1 (out_7, Overflow_AND, Overflow_SUB);
  Comparator #(.width(32)) comparator_1 (.a(in_2), .b(in_3), .gt(A_Larger), .lt(B_Larger));  // open: eq
  Comparator #(.width(32)) comparator_2 (.a(in_2), .b({32{1'b0}}), .gt(P_IN1), .lt(N_IN1));  // open: eq
  Comparator #(.width(32)) comparator_3 (.a(in_3), .b({32{1'b0}}), .gt(P_IN2), .lt(N_IN2));  // open: eq
  Comparator #(.width(32)) comparator_4 (.a(ANDOUT), .b({32{1'b0}}), .gt(PANDOUT), .lt(NANDOUT));  // open: eq
  Comparator #(.width(32)) comparator_5 (.a(SUBOUT), .b({32{1'b0}}), .gt(PSUBOUT), .lt(NSUBOUT));  // open: eq
  Adder #(.width(32)) adder_1 (.a(in_2), .b(in_3), .out(ANDOUT));  // open: cin, cout
  Subtractor #(.width(32)) subtractor_1 (.a(in_2), .b(in_3), .out(SUBOUT));  // open: bin, bout
  Multiplier #(.width(31)) multiplier_1 (.a(in_2[30:0]), .b(in_3[30:0]), .out(MULOUT[30:0]));  // open: cin, cout
  xor xor_1 (MULOUT[31], in_2[31], in_3[31]);
  and and_1 (and_1_out, P_IN1, P_IN2, NANDOUT);
  and and_2 (and_2_out, N_IN1, N_IN2, PANDOUT);
  and and_3 (and_3_out, A_Larger, NSUBOUT);
  and and_4 (and_4_out, B_Larger, PSUBOUT);
  or or_2 (or_2_out, and_3_out, and_4_out);
  or or_3 (or_3_out, and_1_out, and_2_out);
  and and_5 (Overflow_SUB, in_5, or_2_out);
  and and_6 (Overflow_AND, in_1, or_3_out);
  Multiplexer #(.select(2), .width(32), .enable("false")) multiplexer_1 (
    .in0(ANDOUT), .in1(SUBOUT), .in2(MULOUT), .out(out_6), .sel(in_4));  // open: in3

  // Other names for the same wires on the sheet: IN1[31:0] = in_2; IN2[31:0] = in_3

  // Notes on the sheet:
  //   add
  //   sub
endmodule
