// Logisim project Comparator.circ as structural Verilog: 1 circuit, main circuit main
module main (
  input  [31:0] in_1,
  input  [31:0] in_2,
  input  [1:0] in_3,
  output out_4,
  output out_5,
  output out_6,
  output out_7,
  output out_8,
  output out_9
);

  wire comparator_1_gt, comparator_2_eq, comparator_2_gt;

  Multiplexer #(.select(2), .enable("false")) multiplexer_1 (
    .in0(out_6), .in1(out_5), .in2(out_9), .out(out_7), .sel(in_3));  // open: in3
  Comparator #(.width(32)) comparator_1 (.a(in_1), .b(in_2), .gt(comparator_1_gt), .eq(out_5), .lt(out_6));
  Comparator #(.width(32), .mode("unsigned")) comparator_2 (
    .a(in_1), .b(in_2), .gt(comparator_2_gt), .eq(comparator_2_eq), .lt(out_9));
  or or_1 (out_4, comparator_1_gt, out_5);
  or or_2 (out_8, comparator_2_gt, comparator_2_eq);

  // Other names for the same wires on the sheet: Greater_Equal = out_4; Greater_Equal_Unsigned = out_8;
  //   RS1[31:0] = in_1; RS2_Imm16[31:0] = in_2; Equal_NotEqual = out_5; SEQ = out_5; SLT = out_6; Smaller = out_6;
  //   Smaller_Unsigned = out_9; Unsigned_SLT = out_9
endmodule
