// Logisim project Shifter.circ as structural Verilog: 1 circuit, main circuit main
module main (
  input  [31:0] in_1,
  input  [1:0] in_2,
  input  [4:0] in_3,
  output [31:0] out_4
);

  wire [31:0] OutROR, OutSLL, OutSRA, OutSRL;

  Shifter #(.width(32)) shifter_1 (.in(in_1), .\dist (in_3), .out(OutSLL));
  Shifter #(.width(32), .shift("lr")) shifter_2 (.in(in_1), .\dist (in_3), .out(OutSRL));
  Shifter #(.width(32), .shift("ar")) shifter_3 (.in(in_1), .\dist (in_3), .out(OutSRA));
  Shifter #(.width(32), .shift("rr")) shifter_4 (.in(in_1), .\dist (in_3), .out(OutROR));
  Multiplexer #(.select(2), .width(32), .enable("false")) multiplexer_1 (
    .in0(OutSLL), .in1(OutSRL), .in2(OutSRA), .in3(OutROR), .out(out_4), .sel(in_2));

  // Other names for the same wires on the sheet: IN1[31:0] = in_1; IN2[4:0] = in_3
endmodule
