// Logisim project MULF.circ as structural Verilog: 1 circuit, main circuit main
module main (
  input  [31:0] in_1,
  input  [31:0] in_2,
  output [31:0] out_3
);

  Multiplier #(.width(31)) multiplier_1 (.a(in_1[30:0]), .b(in_2[30:0]), .out(out_3[30:0]));  // open: cin, cout
  xor xor_1 (out_3[31], in_1[31], in_2[31]);
endmodule
