// Logisim project final_multiplier.circ as structural Verilog: 1 circuit, main circuit main
module main (
  input  [31:0] in_1,
  input  [31:0] in_2,
  output [31:0] out_3
);

  wire [15:0] multiplier_1_cout, multiplier_1_out, multiplier_2_cout, multiplier_2_out, multiplier_3_cout,
       multiplier_3_out, multiplier_4_cout, multiplier_4_out;
  wire [31:0] adder_1_out, adder_2_out, adder_3_out, adder_4_out, adder_5_out, adder_6_out,
       bit_extender_1_out, bit_extender_2_out, bit_extender_3_out, bit_extender_4_out, bit_extender_5_out,
       bit_extender_6_out, bit_extender_7_out, bit_extender_8_out, shifter_1_out, shifter_2_out,
       shifter_3_out, shifter_4_out, shifter_5_out, shifter_6_out;

  Multiplier #(.width(16)) multiplier_1 (
    .a(in_1[15:0]), .b(in_2[15:0]), .out(multiplier_1_out), .cout(multiplier_1_cout));  // open: cin
  Multiplier #(.width(16)) multiplier_2 (
    .a(in_1[31:16]), .b(in_2[15:0]), .out(multiplier_2_out), .cout(multiplier_2_cout));  // open: cin
  Multiplier #(.width(16)) multiplier_3 (
    .a(in_1[15:0]), .b(in_2[31:16]), .out(multiplier_3_out), .cout(multiplier_3_cout));  // open: cin
  Multiplier #(.width(16)) multiplier_4 (
    .a(in_1[31:16]), .b(in_2[31:16]), .out(multiplier_4_out), .cout(multiplier_4_cout));  // open: cin
  assign bit_extender_1_out = {{16{1'b0}}, multiplier_1_cout};  // Bit_Extender bit_extender_1
  assign bit_extender_2_out = {{16{1'b0}}, multiplier_2_cout};  // Bit_Extender bit_extender_2
  assign bit_extender_3_out = {{16{1'b0}}, multiplier_3_cout};  // Bit_Extender bit_extender_3
  assign bit_extender_4_out = {{16{1'b0}}, multiplier_4_cout};  // Bit_Extender bit_extender_4
  assign bit_extender_5_out = {{16{1'b0}}, multiplier_1_out};  // Bit_Extender bit_extender_5
  Shifter #(.width(32)) shifter_1 (.in(bit_extender_1_out), .\dist (5'b10000), .out(shifter_1_out));
  assign bit_extender_6_out = {{16{1'b0}}, multiplier_2_out};  // Bit_Extender bit_extender_6
  Shifter #(.width(32)) shifter_2 (.in(bit_extender_2_out), .\dist (5'b10000), .out(shifter_2_out));
  assign bit_extender_7_out = {{16{1'b0}}, multiplier_3_out};  // Bit_Extender bit_extender_7
  Shifter #(.width(32)) shifter_3 (.in(bit_extender_3_out), .\dist (5'b10000), .out(shifter_3_out));
  assign bit_extender_8_out = {{16{1'b0}}, multiplier_4_out};  // Bit_Extender bit_extender_8
  Shifter #(.width(32)) shifter_4 (.in(bit_extender_4_out), .\dist (5'b10000), .out(shifter_4_out));
  Adder #(.width(32)) adder_1 (.a(bit_extender_5_out), .b(shifter_1_out), .out(adder_1_out));  // open: cin, cout
  Adder #(.width(32)) adder_2 (.a(bit_extender_6_out), .b(shifter_2_out), .out(adder_2_out));  // open: cin, cout
  Adder #(.width(32)) adder_3 (.a(bit_extender_7_out), .b(shifter_3_out), .out(adder_3_out));  // open: cin, cout
  Adder #(.width(32)) adder_4 (.a(bit_extender_8_out), .b(shifter_4_out), .out(adder_4_out));  // open: cin, cout
  Shifter #(.width(32)) shifter_5 (.in(adder_2_out), .\dist (5'b10000), .out(shifter_5_out));
  Shifter #(.width(32)) shifter_6 (.in(adder_3_out), .\dist (5'b10000), .out(shifter_6_out));
  Adder #(.width(32)) adder_5 (.a(adder_1_out), .b(shifter_5_out), .out(adder_5_out));  // open: cin, cout
  Adder #(.width(32)) adder_6 (.a(shifter_6_out), .b(adder_4_out), .out(adder_6_out));  // open: cin, cout
  Adder #(.width(32)) adder_7 (.a(adder_5_out), .b(adder_6_out), .out(out_3));  // open: cin, cout

  // Other names for the same wires on the sheet: A_LO[15:0] = in_1[15:0]; A_HI[15:0] = in_1[31:16];
  //   B_LO[15:0] = in_2[15:0]; B_HI[15:0] = in_2[31:16]

  // Notes on the sheet:
  //   A
  //   B
endmodule
