// Logisim project AlUt.circ as structural Verilog: 3 circuits, main circuit ARTHIm
module main (
  input  in_1,
  input  [31:0] in_2,
  input  in_3,
  input  [31:0] in_4,
  input  in_5,
  output [31:0] out_6,
  output out_7
);

  wire A_Larger, and_1_out, and_2_out, and_3_out, and_4_out, B_Larger, N_IN1, N_IN2, NANDOUT, NSUBOUT,
       or_2_out, or_3_out, Overflow_AND, Overflow_SUB, P_IN1, P_IN2, PANDOUT, PSUBOUT;
  wire [31:0] ANDOUT, SUBOUT;

  or or_1 (out_7, Overflow_AND, Overflow_SUB);
  Comparator #(.width(32)) comparator_1 (.a(in_2), .b(in_4), .gt(A_Larger), .lt(B_Larger));  // open: eq
  Comparator #(.width(32)) comparator_2 (.a(in_2), .b({32{1'b0}}), .gt(P_IN1), .lt(N_IN1));  // open: eq
  Comparator #(.width(32)) comparator_3 (.a(in_4), .b({32{1'b0}}), .gt(P_IN2), .lt(N_IN2));  // open: eq
  Comparator #(.width(32)) comparator_4 (.a(ANDOUT), .b({32{1'b0}}), .gt(PANDOUT), .lt(NANDOUT));  // open: eq
  Comparator #(.width(32)) comparator_5 (.a(SUBOUT), .b({32{1'b0}}), .gt(PSUBOUT), .lt(NSUBOUT));  // open: eq
  Adder #(.width(32)) adder_1 (.a(in_2), .b(in_4), .out(ANDOUT));  // open: cin, cout
  Subtractor #(.width(32)) subtractor_1 (.a(in_2), .b(in_4), .out(SUBOUT));  // open: bin, bout
  and and_1 (and_1_out, P_IN1, P_IN2, NANDOUT);
  and and_2 (and_2_out, N_IN1, N_IN2, PANDOUT);
  and and_3 (and_3_out, A_Larger, NSUBOUT);
  and and_4 (and_4_out, B_Larger, PSUBOUT);
  Multiplexer #(.width(32), .enable("false")) multiplexer_1 (.in0(ANDOUT), .in1(SUBOUT), .out(out_6), .sel(in_3));
  or or_2 (or_2_out, and_3_out, and_4_out);
  or or_3 (or_3_out, and_1_out, and_2_out);
  and and_5 (Overflow_SUB, in_5, or_2_out);
  and and_6 (Overflow_AND, in_1, or_3_out);

  // Other names for the same wires on the sheet: IN1[31:0] = in_2; IN2[31:0] = in_4

  // Notes on the sheet:
  //   add
  //   sub
endmodule

module ARTHIm (
  input  [31:0] in_1,
  input  [31:0] in_2,
  input  [4:0] in_3,
  input  in_4,
  input  in_5,
  input  [1:0] in_6,
  input  [1:0] in_7,
  input  [1:0] in_8,
  input  [1:0] in_9,
  input  [1:0] in_10,
  output out_11,
  output out_12,
  output out_13,
  output out_14,
  output [31:0] out_15,
  output out_16,
  output out_17,
  output out_18,
  output out_19
);

  wire [31:0] main_1_out_4, main_2_p7, main_3_out_4, main_4_out_9;

  Shifter_main main_1 (.in_1(in_1), .in_3(in_3), .in_2(in_8), .out_4(main_1_out_4));
  // Arith_unit_main main_2: pin names not known; wires that end beside it: in_1, in_2, in_4, in_5, in_6, out_14, main_2_p7
  logical_unit_main main_3 (.in_1(in_1), .in_2(in_2), .out_4(main_3_out_4), .in_3(in_7));
  Comparator_main main_4 (
    .in_1(in_1), .in_2(in_2), .out_4(out_18), .out_5(out_16), .out_6(out_11), .out_9(main_4_out_9),
    .out_7(out_19), .out_8(out_13), .in_3(in_9));
  Multiplexer #(.select(2), .width(32), .enable("false")) multiplexer_1 (
    .in0(main_2_p7), .in1(main_3_out_4), .in2(main_1_out_4), .in3(main_4_out_9), .out(out_15), .sel(in_10));
  main main_5 ();  // open: in_2, in_4, out_6, in_3, out_7, in_1, in_5

  assign out_12 = out_11;
  assign out_17 = out_16;

  // Other names for the same wires on the sheet: ALUresult[31:0] = out_15; Overflow = out_14; RS1[31:0] = in_1;
  //   RS2[31:0] = in_2; SA_RS2[4:0] = in_3; select_operation[1:0] = in_10; signal_AND = in_4;
  //   signal_Eq_NotEq = out_16; signal_Greater_Eq = out_18; signal_Greater_Eq_Unsigned = out_19;
  //   signal_select_Arth_op[1:0] = in_6; signal_Select_comp_op[1:0] = in_9; signal_select_logic_op[1:0] = in_7;
  //   signal_select_shift_op[1:0] = in_8; signal_smaller = out_11; signal_smaller_unsigned = out_13;
  //   signal_sub = in_5
endmodule

module ALU (
);

  ARTHIm arthim_1 ();  // open: out_18, out_19, out_13, in_9, in_7, in_8, in_10, in_6, in_4, in_5, out_14, out_15, out_17, out_12, in_1, in_2, in_3
  ARTHIm arthim_2 ();  // open: out_18, out_19, out_13, in_9, in_7, in_8, in_10, in_6, in_4, in_5, out_14, out_15, out_17, out_12, in_1, in_2, in_3
endmodule
