// Logisim project Alu.circ as structural Verilog: 1 circuit, main circuit main
module main (
  input  [31:0] in_1,
  input  [31:0] in_2,
  input  [4:0] in_3,
  input  in_4,
  input  in_5,
  input  [1:0] in_6,
  input  [1:0] in_7,
  input  [1:0] in_8,
  input  [1:0] in_9,
  input  [1:0] in_10,
  output out_11,
  output out_12,
  output out_13,
  output [31:0] out_14,
  output out_15,
  output out_16,
  output out_17
);

  wire [31:0] main_1_out_4, main_2_p7, main_3_out_4, main_4_out_9;

  Shifter_main main_1 (.in_1(in_1), .in_3(in_3), .in_2(in_8), .out_4(main_1_out_4));
  // Arith_unit_main main_2: pin names not known; wires that end beside it: in_1, in_2, in_4, in_5, in_6, out_13, main_2_p7
  logical_unit_main main_3 (.in_1(in_1), .in_2(in_2), .out_4(main_3_out_4), .in_3(in_7));
  Comparator_main main_4 (
    .in_1(in_1), .in_2(in_2), .out_4(out_16), .out_5(out_15), .out_6(out_11), .out_9(main_4_out_9),
    .out_7(out_17), .out_8(out_12), .in_3(in_9));
  Multiplexer #(.select(2), .width(32), .enable("false")) multiplexer_1 (
    .in0(main_2_p7), .in1(main_3_out_4), .in2(main_1_out_4), .in3(main_4_out_9), .out(out_14), .sel(in_10));

  // Other names for the same wires on the sheet: ALUresult[31:0] = out_14; Overflow = out_13; RS1[31:0] = in_1;
  //   RS2[31:0] = in_2; SA_RS2[4:0] = in_3; select_operation[1:0] = in_10; signal_AND = in_4;
  //   signal_Eq_NotEq = out_15; signal_Greater_Eq = out_16; signal_Greater_Eq_Unsigned = out_17;
  //   signal_select_Arth_op[1:0] = in_6; signal_Select_comp_op[1:0] = in_9; signal_select_logic_op[1:0] = in_7;
  //   signal_select_shift_op[1:0] = in_8; signal_smaller = out_11; signal_smaller_unsigned = out_12;
  //   signal_sub = in_5
endmodule
