// Logisim project EX_MEM.circ as structural Verilog: 1 circuit, main circuit main
module main (
  input  [19:0] in_1,
  input  in_2,
  input  in_3,
  input  in_4,
  input  in_5,
  input  in_6,
  input  in_7,
  input  [31:0] in_8,
  input  [31:0] in_9,
  input  [31:0] in_10,
  input  [31:0] in_11,
  input  [31:0] in_12,
  input  [4:0] in_13,
  input  in_14,
  input  in_15,
  input  [1:0] in_16,
  input  in_17,
  input  in_18,
  output [19:0] out_19,
  output out_20,
  output out_21,
  output out_22,
  output out_23,
  output out_24,
  output [4:0] out_25,
  output [31:0] out_26,
  output [31:0] out_27,
  output [31:0] out_28,
  output [31:0] out_29,
  output [31:0] out_30,
  output out_31,
  output out_32,
  output [1:0] out_33,
  output out_34,
  output out_35
);

  Register #(.width(20)) register_1 (.D(in_1), .en(1'b1), .clk(in_2), .Q(out_19));  // open: clr
  Register #(.width(5)) register_2 (
    .D({in_7, in_6, in_5, in_4, in_3}), .en(1'b1), .clk(in_2), .Q({out_24, out_23, out_22, out_21, out_20}));  // open: clr
  Register #(.width(32)) register_3 (.D(in_8), .en(1'b1), .clk(in_2), .Q(out_26));  // open: clr
  Register #(.width(32)) register_4 (.D(in_9), .en(1'b1), .clk(in_2), .Q(out_27));  // open: clr
  Register #(.width(32)) register_5 (.D(in_10), .en(1'b1), .clk(in_2), .Q(out_28));  // open: clr
  Register #(.width(32)) register_6 (.D(in_11), .en(1'b1), .clk(in_2), .Q(out_29));  // open: clr
  Register #(.width(32)) register_7 (.D(in_12), .en(1'b1), .clk(in_2), .Q(out_30));  // open: clr
  Register #(.width(5)) register_8 (.D(in_13), .en(in_2), .clk(1'b1), .Q(out_25));  // open: clr
  Register #(.width(6)) register_9 (
    .D({in_18, in_17, in_16, in_15, in_14}), .en(1'b1), .clk(in_2),
    .Q({out_35, out_34, out_33, out_32, out_31}));  // open: clr

  // Other names for the same wires on the sheet: BLT = out_20; BLTU = out_21; BEQ_BNE = out_22; BGE = out_23;
  //   BGEU = out_24; MemRead = out_31; MemWrite = out_32; MUX_RD_1[1:0] = out_33; MUX_RD_2 = out_34;
  //   RegWrite = out_35; ALU_res[31:0] = out_26; Branch[19:0] = out_19; CLK = in_2; PC_1[31:0] = out_30;
  //   RD[4:0] = out_25; RS2[31:0] = out_27; SET[31:0] = out_28; SSET[31:0] = out_29
endmodule
