// Logisim project ID_EX.circ as structural Verilog: 1 circuit, main circuit main
module main (
  input  [31:0] in_1,
  input  [31:0] in_2,
  input  [31:0] in_3,
  input  [4:0] in_4,
  input  [31:0] in_5,
  input  [31:0] in_6,
  input  [19:0] in_7,
  input  [31:0] in_8,
  input  Signal_of_add,
  input  Signal_of_Sub,
  input  Reg_Write,
  input  Mux_SA_RS2,
  input  Mux_RD2,
  input  MEM_Read,
  input  MEM_Write,
  input  [1:0] Mux_RD_1,
  input  [1:0] Arith_op,
  input  [1:0] Logical_op,
  input  [1:0] Comprator_op,
  input  [1:0] Shifter_op,
  input  CLK,
  input  [1:0] ALU_op,
  output [31:0] out_23,
  output [31:0] out_24,
  output [31:0] out_25,
  output [4:0] out_26,
  output [31:0] out_27,
  output [31:0] out_28,
  output [19:0] out_29,
  output [31:0] out_30,
  output Signal_of_add_2,
  output Signal_of_Sub_2,
  output Reg_Write_2,
  output Mux_SA_RS2_2,
  output Mux_RD2_2,
  output MEM_Read_2,
  output MEM_Write_2,
  output [1:0] Mux_RD_1_2,
  output [1:0] Arith_op_2,
  output [1:0] Logical_op_2,
  output [1:0] Comprator_op_2,
  output [1:0] Shifter_op_2,
  output [1:0] ALU_op_2
);

  Register #(.width(32)) BusS1 (.D(in_1), .en(1'b1), .clk(CLK), .Q(out_23));  // open: clr
  Register #(.width(32)) BusS2 (.D(in_2), .en(1'b1), .clk(CLK), .Q(out_24));  // open: clr
  Register #(.width(32)) MuxRs2 (.D(in_3), .en(1'b1), .clk(CLK), .Q(out_25));  // open: clr
  Register #(.width(5)) RD (.D(in_4), .en(1'b1), .clk(CLK), .Q(out_26));  // open: clr
  Register #(.width(32)) SET (.D(in_5), .en(1'b1), .clk(CLK), .Q(out_27));  // open: clr
  Register #(.width(32)) SSET (.D(in_6), .en(1'b1), .clk(CLK), .Q(out_28));  // open: clr
  Register #(.width(20)) Branch_address (.D(in_7), .en(1'b1), .clk(CLK), .Q(out_29));  // open: clr
  Register #(.width(32)) PC_1 (.D(in_8), .en(1'b1), .clk(CLK), .Q(out_30));  // open: clr
  Register #(.width(7)) Signals_1bit (
    .D({MEM_Write, MEM_Read, Mux_RD2, Mux_SA_RS2, Reg_Write, Signal_of_Sub, Signal_of_add}), .en(1'b1),
    .clk(CLK),
    .Q({MEM_Write_2, MEM_Read_2, Mux_RD2_2, Mux_SA_RS2_2, Reg_Write_2, Signal_of_Sub_2, Signal_of_add_2}));  // open: clr
  Register #(.width(12)) Signals_2bit (
    .D({ALU_op, Shifter_op, Comprator_op, Logical_op, Arith_op, Mux_RD_1}), .en(1'b1), .clk(CLK),
    .Q({ALU_op_2, Shifter_op_2, Comprator_op_2, Logical_op_2, Arith_op_2, Mux_RD_1_2}));  // open: clr
endmodule
