// Logisim project Inst_memory.circ as structural Verilog
module main (
  input  [19:0] in_1,
  output [15:0] out_2,
  output [4:0] out_3,
  output [5:0] out_4,
  output [4:0] out_5,
  output [4:0] out_6,
  output [10:0] out_7,
  output [4:0] out_8,
  output [4:0] out_9
);

  ROM #(.addrWidth(20), .dataWidth(32)) rom_1 (.addr(in_1), .data({out_2, out_8, out_5, out_4}));

  assign out_3 = out_2[4:0];
  assign out_6 = out_5;
  assign out_7 = out_2[15:5];
  assign out_9 = out_8;

  // Other names for the same wires on the sheet: op[5:0] = out_4; d1[4:0] = out_5; ImmL[4:0] = out_5; s1[4:0] = out_8;
  //   Imm16[15:0] = out_2; s2[4:0] = out_2[4:0]; F11[10:0] = out_2[15:5]; ImmU[10:0] = out_2[15:5]; PC[19:0] = in_1
endmodule
