// Logisim project MEM_WB.circ as structural Verilog: 1 circuit, main circuit main
module main (
  input  [31:0] in_1,
  input  in_2,
  input  [4:0] in_3,
  input  in_4,
  output [31:0] out_5,
  output [4:0] out_6,
  output out_7
);

  Register #(.width(32)) register_1 (.D(in_1), .en(in_2), .clk(1'b1), .Q(out_5));  // open: clr
  Register #(.width(5)) register_2 (.D(in_3), .en(in_2), .clk(1'b1), .Q(out_6));  // open: clr
  Register #(.width(1)) register_3 (.D(in_4), .en(1'b1), .clk(in_2), .Q(out_7));  // open: clr

  // Other names for the same wires on the sheet: BusD[31:0] = out_5; CLK = in_2; RD[4:0] = out_6; RegWrite = out_7
endmodule
