// Logisim project RF.circ as structural Verilog
module main (
  input  [4:0] RA,
  input  [4:0] RB,
  input  [4:0] RW,
  input  [31:0] in_4,
  input  in_5,
  input  in_6,
  output [31:0] out_7,
  output [31:0] out_8,
  output [31:0] out_9,
  output [31:0] out_10,
  output [31:0] out_11,
  output [31:0] out_12,
  output [31:0] out_13,
  output [31:0] out_14,
  output [31:0] out_15,
  output [31:0] out_16,
  output [31:0] out_17,
  output [31:0] out_18,
  output [31:0] out_19,
  output [31:0] out_20,
  output [31:0] out_21,
  output [31:0] out_22,
  output [31:0] out_23,
  output [31:0] out_24,
  output [31:0] out_25,
  output [31:0] out_26,
  output [31:0] out_27,
  output [31:0] out_28,
  output [31:0] out_29,
  output [31:0] out_30,
  output [31:0] out_31,
  output [31:0] out_32,
  output [31:0] out_33,
  output [31:0] out_34,
  output [31:0] out_35,
  output [31:0] out_36,
  output [31:0] out_37,
  output [31:0] out_38,
  output [31:0] out_39,
  output [31:0] out_40
);

  wire A0, A1, A2, A3, A4, A5, A6, A7, A8, A9, A10, A11, A12, A13, A14, A15, A16, A17, A18, A19, A20, A21,
       A22, A23, A24, A25, A26, A27, A28, A29, A30, A31, and_1_out, and_2_out, and_3_out, and_4_out,
       and_5_out, and_6_out, and_7_out, and_8_out, and_9_out, and_10_out, and_11_out, and_12_out, and_13_out,
       and_14_out, and_15_out, and_16_out, and_17_out, and_18_out, and_19_out, and_20_out, and_21_out,
       and_22_out, and_23_out, and_24_out, and_25_out, and_26_out, and_27_out, and_28_out, and_29_out,
       and_30_out, and_31_out, and_32_out, B0, B1, B2, B3, B4, B5, B6, B7, B8, B9, B10, B11, B12, B13, B14,
       B15, B16, B17, B18, B19, B20, B21, B22, B23, B24, B25, B26, B27, B28, B29, B30, B31, Re1, Re2, Re3,
       Re4, Re5, Re6, Re7, Re8, Re9, Re10, Re11, Re12, Re13, Re14, Re15, Re16, Re17, Re18, Re19, Re20, Re21,
       Re22, Re23, Re24, Re25, Re26, Re27, Re28, Re29, Re30, Re31;

  Decoder #(.select(5), .enable("false")) decoder_1 (
    .out1(Re1), .out2(Re2), .out3(Re3), .out4(Re4), .out5(Re5), .out6(Re6), .out7(Re7), .out8(Re8),
    .out9(Re9), .out10(Re10), .out11(Re11), .out12(Re12), .out13(Re13), .out14(Re14), .out15(Re15),
    .out16(Re16), .out17(Re17), .out18(Re18), .out19(Re19), .out20(Re20), .out21(Re21), .out22(Re22),
    .out23(Re23), .out24(Re24), .out25(Re25), .out26(Re26), .out27(Re27), .out28(Re28), .out29(Re29),
    .out30(Re30), .out31(Re31), .sel(RW));  // open: out0
  and and_1 (and_1_out, 1'b0, in_5);
  and and_2 (and_2_out, Re1, in_5);
  and and_3 (and_3_out, Re2, in_5);
  and and_4 (and_4_out, Re3, in_5);
  and and_5 (and_5_out, Re4, in_5);
  and and_6 (and_6_out, Re5, in_5);
  and and_7 (and_7_out, Re6, in_5);
  Register #(.width(32)) R0 (.D(in_4), .en(and_1_out), .clk(in_6), .Q(out_9));  // open: clr
  Register #(.width(32)) R1 (.D(in_4), .en(and_2_out), .clk(in_6), .Q(out_10));  // open: clr
  Register #(.width(32)) R2 (.D(in_4), .en(and_3_out), .clk(in_6), .Q(out_11));  // open: clr
  Register #(.width(32)) R3 (.D(in_4), .en(and_4_out), .clk(in_6), .Q(out_12));  // open: clr
  Register #(.width(32)) R4 (.D(in_4), .en(and_5_out), .clk(in_6), .Q(out_13));  // open: clr
  Register #(.width(32)) R5 (.D(in_4), .en(and_6_out), .clk(in_6), .Q(out_14));  // open: clr
  Register #(.width(32)) R6 (.D(in_4), .en(and_7_out), .clk(in_6), .Q(out_15));  // open: clr
  Register #(.width(32)) R7 (.D(in_4), .en(and_8_out), .clk(in_6), .Q(out_16));  // open: clr
  and and_8 (and_8_out, Re7, in_5);
  Register #(.width(32)) R8 (.D(in_4), .en(and_9_out), .clk(in_6), .Q(out_17));  // open: clr
  and and_9 (and_9_out, Re8, in_5);
  Register #(.width(32)) R9 (.D(in_4), .en(and_10_out), .clk(in_6), .Q(out_18));  // open: clr
  and and_10 (and_10_out, Re9, in_5);
  Register #(.width(32)) R10 (.D(in_4), .en(and_11_out), .clk(in_6), .Q(out_19));  // open: clr
  and and_11 (and_11_out, Re10, in_5);
  Register #(.width(32)) R11 (.D(in_4), .en(and_12_out), .clk(in_6), .Q(out_20));  // open: clr
  and and_12 (and_12_out, Re11, in_5);
  Register #(.width(32)) R12 (.D(in_4), .en(and_13_out), .clk(in_6), .Q(out_21));  // open: clr
  and and_13 (and_13_out, Re12, in_5);
  Register #(.width(32)) R13 (.D(in_4), .en(and_14_out), .clk(in_6), .Q(out_22));  // open: clr
  and and_14 (and_14_out, Re13, in_5);
  Decoder #(.select(5), .enable("false")) decoder_2 (
    .out0(A0), .out1(A1), .out2(A2), .out3(A3), .out4(A4), .out5(A5), .out6(A6), .out7(A7), .out8(A8),
    .out9(A9), .out10(A10), .out11(A11), .out12(A12), .out13(A13), .out14(A14), .out15(A15), .out16(A16),
    .out17(A17), .out18(A18), .out19(A19), .out20(A20), .out21(A21), .out22(A22), .out23(A23), .out24(A24),
    .out25(A25), .out26(A26), .out27(A27), .out28(A28), .out29(A29), .out30(A30), .out31(A31), .sel(RA));
  Register #(.width(32)) R14 (.D(in_4), .en(and_15_out), .clk(in_6), .Q(out_23));  // open: clr
  and and_15 (and_15_out, Re14, in_5);
  Register #(.width(32)) R15 (.D(in_4), .en(and_16_out), .clk(in_6), .Q(out_24));  // open: clr
  and and_16 (and_16_out, Re15, in_5);
  Register #(.width(32)) R16 (.D(in_4), .en(and_17_out), .clk(in_6), .Q(out_25));  // open: clr
  and and_17 (and_17_out, Re16, in_5);
  Register #(.width(32)) R17 (.D(in_4), .en(and_18_out), .clk(in_6), .Q(out_26));  // open: clr
  and and_18 (and_18_out, Re17, in_5);
  Register #(.width(32)) R18 (.D(in_4), .en(and_19_out), .clk(in_6), .Q(out_27));  // open: clr
  and and_19 (and_19_out, Re18, in_5);
  Register #(.width(32)) R19 (.D(in_4), .en(and_20_out), .clk(in_6), .Q(out_28));  // open: clr
  and and_20 (and_20_out, Re19, in_5);
  Register #(.width(32)) R20 (.D(in_4), .en(and_21_out), .clk(in_6), .Q(out_29));  // open: clr
  and and_21 (and_21_out, Re20, in_5);
  and and_22 (and_22_out, Re21, in_5);
  and and_23 (and_23_out, Re22, in_5);
  and and_24 (and_24_out, Re23, in_5);
  and and_25 (and_25_out, Re24, in_5);
  and and_26 (and_26_out, Re25, in_5);
  and and_27 (and_27_out, Re26, in_5);
  and and_28 (and_28_out, Re27, in_5);
  Register #(.width(32)) R21 (.D(in_4), .en(and_22_out), .clk(in_6), .Q(out_30));  // open: clr
  Register #(.width(32)) R22 (.D(in_4), .en(and_23_out), .clk(in_6), .Q(out_31));  // open: clr
  Register #(.width(32)) R23 (.D(in_4), .en(and_24_out), .clk(in_6), .Q(out_32));  // open: clr
  Register #(.width(32)) R24 (.D(in_4), .en(and_25_out), .clk(in_6), .Q(out_33));  // open: clr
  Register #(.width(32)) R25 (.D(in_4), .en(and_26_out), .clk(in_6), .Q(out_34));  // open: clr
  Register #(.width(32)) R26 (.D(in_4), .en(and_27_out), .clk(in_6), .Q(out_35));  // open: clr
  Register #(.width(32)) R27 (.D(in_4), .en(and_28_out), .clk(in_6), .Q(out_36));  // open: clr
  Decoder #(.select(5), .enable("false")) decoder_3 (
    .out0(B0), .out1(B1), .out2(B2), .out3(B3), .out4(B4), .out5(B5), .out6(B6), .out7(B7), .out8(B8),
    .out9(B9), .out10(B10), .out11(B11), .out12(B12), .out13(B13), .out14(B14), .out15(B15), .out16(B16),
    .out17(B17), .out18(B18), .out19(B19), .out20(B20), .out21(B21), .out22(B22), .out23(B23), .out24(B24),
    .out25(B25), .out26(B26), .out27(B27), .out28(B28), .out29(B29), .out30(B30), .out31(B31), .sel(RB));
  and and_29 (and_29_out, Re28, in_5);
  and and_30 (and_30_out, Re29, in_5);
  and and_31 (and_31_out, Re30, in_5);
  and and_32 (and_32_out, Re31, in_5);
  Register #(.width(32)) R28 (.D(in_4), .en(and_29_out), .clk(in_6), .Q(out_37));  // open: clr
  Register #(.width(32)) R29 (.D(in_4), .en(and_30_out), .clk(in_6), .Q(out_38));  // open: clr
  Register #(.width(32)) R30 (.D(in_4), .en(and_31_out), .clk(in_6), .Q(out_39));  // open: clr
  Register #(.width(32)) R31 (.D(in_4), .en(and_32_out), .clk(in_6), .Q(out_40));  // open: clr
  assign out_7 = A1 ? out_10 : 32'bz;  // Controlled_Buffer R1_2
  assign out_7 = A2 ? out_11 : 32'bz;  // Controlled_Buffer R2_2
  assign out_7 = A3 ? out_12 : 32'bz;  // Controlled_Buffer R3_2
  assign out_7 = A4 ? out_13 : 32'bz;  // Controlled_Buffer R4_2
  assign out_7 = A5 ? out_14 : 32'bz;  // Controlled_Buffer R5_2
  assign out_7 = A6 ? out_15 : 32'bz;  // Controlled_Buffer R6_2
  assign out_7 = A7 ? out_16 : 32'bz;  // Controlled_Buffer R7_2
  assign out_7 = A8 ? out_17 : 32'bz;  // Controlled_Buffer R8_2
  assign out_7 = A9 ? out_18 : 32'bz;  // Controlled_Buffer R9_2
  assign out_7 = A10 ? out_19 : 32'bz;  // Controlled_Buffer R10_2
  assign out_8 = B1 ? out_10 : 32'bz;  // Controlled_Buffer R1_3
  assign out_8 = B2 ? out_11 : 32'bz;  // Controlled_Buffer R2_3
  assign out_8 = B3 ? out_12 : 32'bz;  // Controlled_Buffer R3_3
  assign out_8 = B4 ? out_13 : 32'bz;  // Controlled_Buffer R4_3
  assign out_8 = B5 ? out_14 : 32'bz;  // Controlled_Buffer R5_3
  assign out_8 = B6 ? out_15 : 32'bz;  // Controlled_Buffer R6_3
  assign out_8 = B7 ? out_16 : 32'bz;  // Controlled_Buffer R7_3
  assign out_8 = B8 ? out_17 : 32'bz;  // Controlled_Buffer R8_3
  assign out_8 = B9 ? out_18 : 32'bz;  // Controlled_Buffer R9_3
  assign out_8 = B10 ? out_19 : 32'bz;  // Controlled_Buffer R10_3
  assign out_7 = A0 ? {32{1'b0}} : 32'bz;  // Controlled_Buffer R0_2
  assign out_7 = A21 ? out_30 : 32'bz;  // Controlled_Buffer R21_2
  assign out_7 = A22 ? out_31 : 32'bz;  // Controlled_Buffer R22_2
  assign out_7 = A23 ? out_32 : 32'bz;  // Controlled_Buffer R23_2
  assign out_7 = A24 ? out_33 : 32'bz;  // Controlled_Buffer R24_2
  assign out_7 = A25 ? out_34 : 32'bz;  // Controlled_Buffer R25_2
  assign out_7 = A26 ? out_35 : 32'bz;  // Controlled_Buffer R26_2
  assign out_7 = A27 ? out_36 : 32'bz;  // Controlled_Buffer R27_2
  assign out_7 = A28 ? out_37 : 32'bz;  // Controlled_Buffer R28_2
  assign out_7 = A29 ? out_38 : 32'bz;  // Controlled_Buffer R29_2
  assign out_7 = A30 ? out_39 : 32'bz;  // Controlled_Buffer R30_2
  assign out_7 = A31 ? out_40 : 32'bz;  // Controlled_Buffer R31_2
  assign out_8 = B0 ? {32{1'b0}} : 32'bz;  // Controlled_Buffer R0_3
  assign out_7 = A11 ? out_20 : 32'bz;  // Controlled_Buffer R11_2
  assign out_7 = A12 ? out_21 : 32'bz;  // Controlled_Buffer R12_2
  assign out_7 = A13 ? out_22 : 32'bz;  // Controlled_Buffer R13_2
  assign out_7 = A14 ? out_23 : 32'bz;  // Controlled_Buffer R14_2
  assign out_7 = A15 ? out_24 : 32'bz;  // Controlled_Buffer R15_2
  assign out_7 = A16 ? out_25 : 32'bz;  // Controlled_Buffer R16_2
  assign out_7 = A17 ? out_26 : 32'bz;  // Controlled_Buffer R17_2
  assign out_7 = A18 ? out_27 : 32'bz;  // Controlled_Buffer R18_2
  assign out_7 = A19 ? out_28 : 32'bz;  // Controlled_Buffer R19_2
  assign out_7 = A20 ? out_29 : 32'bz;  // Controlled_Buffer R20_2
  assign out_8 = B21 ? out_30 : 32'bz;  // Controlled_Buffer R21_3
  assign out_8 = B22 ? out_31 : 32'bz;  // Controlled_Buffer R22_3
  assign out_8 = B23 ? out_32 : 32'bz;  // Controlled_Buffer R23_3
  assign out_8 = B24 ? out_33 : 32'bz;  // Controlled_Buffer R24_3
  assign out_8 = B25 ? out_34 : 32'bz;  // Controlled_Buffer R25_3
  assign out_8 = B26 ? out_35 : 32'bz;  // Controlled_Buffer R26_3
  assign out_8 = B27 ? out_36 : 32'bz;  // Controlled_Buffer R27_3
  assign out_8 = B28 ? out_37 : 32'bz;  // Controlled_Buffer R28_3
  assign out_8 = B29 ? out_38 : 32'bz;  // Controlled_Buffer R29_3
  assign out_8 = B30 ? out_39 : 32'bz;  // Controlled_Buffer R30_3
  assign out_8 = B31 ? out_40 : 32'bz;  // Controlled_Buffer R31_3
  assign out_8 = B11 ? out_20 : 32'bz;  // Controlled_Buffer R11_3
  assign out_8 = B12 ? out_21 : 32'bz;  // Controlled_Buffer R12_3
  assign out_8 = B13 ? out_22 : 32'bz;  // Controlled_Buffer R13_3
  assign out_8 = B14 ? out_23 : 32'bz;  // Controlled_Buffer R14_3
  assign out_8 = B15 ? out_24 : 32'bz;  // Controlled_Buffer R15_3
  assign out_8 = B16 ? out_25 : 32'bz;  // Controlled_Buffer R16_3
  assign out_8 = B17 ? out_26 : 32'bz;  // Controlled_Buffer R17_3
  assign out_8 = B18 ? out_27 : 32'bz;  // Controlled_Buffer R18_3
  assign out_8 = B19 ? out_28 : 32'bz;  // Controlled_Buffer R19_3
  assign out_8 = B20 ? out_29 : 32'bz;  // Controlled_Buffer R20_3

  // Other names for the same wires on the sheet: BusA[31:0] = out_7; BusB[31:0] = out_8; BusW[31:0] = in_4;
  //   clock = in_6; outR0[31:0] = out_9; outR1[31:0] = out_10; Rego1[31:0] = out_10; outR2[31:0] = out_11;
  //   Rego2[31:0] = out_11; outR3[31:0] = out_12; Rego3[31:0] = out_12; outR4[31:0] = out_13; Rego4[31:0] = out_13;
  //   outR5[31:0] = out_14; Rego5[31:0] = out_14; outR6[31:0] = out_15; Rego6[31:0] = out_15; outR7[31:0] = out_16;
  //   Rego7[31:0] = out_16; outR8[31:0] = out_17; Rego8[31:0] = out_17; outR9[31:0] = out_18; Rego9[31:0] = out_18;
  //   outR10[31:0] = out_19; Rego10[31:0] = out_19; outR11[31:0] = out_20; Rego11[31:0] = out_20;
  //   outR12[31:0] = out_21; Rego12[31:0] = out_21; outR13[31:0] = out_22; Rego13[31:0] = out_22;
  //   outR14[31:0] = out_23; Rego14[31:0] = out_23; outR15[31:0] = out_24; Rego15[31:0] = out_24;
  //   outR16[31:0] = out_25; Rego16[31:0] = out_25; outR17[31:0] = out_26; Rego17[31:0] = out_26;
  //   outR18[31:0] = out_27; Rego18[31:0] = out_27; outR19[31:0] = out_28; Rego19[31:0] = out_28;
  //   outR20[31:0] = out_29; Rego20[31:0] = out_29; outR21[31:0] = out_30; Rego21[31:0] = out_30;
  //   outR22[31:0] = out_31; Rego22[31:0] = out_31; outR23[31:0] = out_32; Rego23[31:0] = out_32;
  //   outR24[31:0] = out_33; Rego24[31:0] = out_33; outR25[31:0] = out_34; Rego25[31:0] = out_34;
  //   outR26[31:0] = out_35; Rego26[31:0] = out_35; outR27[31:0] = out_36; Rego27[31:0] = out_36;
  //   outR28[31:0] = out_37; Rego28[31:0] = out_37; outR29[31:0] = out_38; Rego29[31:0] = out_38;
  //   outR30[31:0] = out_39; Rego30[31:0] = out_39; outR31[31:0] = out_40; Rego31[31:0] = out_40; RegWrite = in_5
endmodule
