// Logisim project logical_unit.circ as structural Verilog: 1 circuit, main circuit main
module main (
  input  [31:0] in_1,
  input  [31:0] in_2,
  input  [1:0] in_3,
  output [31:0] out_4
);

  wire [31:0] ANDOUT, NOROUT, OROUT, XOROUT;

  assign ANDOUT = in_1 & in_2;  // AND_Gate and_1, 32 bits wide
  assign OROUT = in_1 | in_2;  // OR_Gate or_1, 32 bits wide
  assign NOROUT = ~(in_1 | in_2);  // NOR_Gate nor_1, 32 bits wide
  assign XOROUT = in_1 ^ in_2;  // XOR_Gate xor_1, 32 bits wide
  Multiplexer #(.select(2), .width(32), .enable("false")) multiplexer_1 (
    .in0(ANDOUT), .in1(OROUT), .in2(NOROUT), .in3(XOROUT), .out(out_4), .sel(in_3));

  // Other names for the same wires on the sheet: IN1[31:0] = in_1; IN2[31:0] = in_2
endmodule
