// Logisim project ALU_control unit.circ as structural Verilog: 1 circuit, main circuit main
module main (
  input  [10:0] in_1,
  input  [5:0] in_2,
  input  in_3,
  output Signal_of_add,
  output Signal_of_sub,
  output [1:0] Arith_op,
  output [1:0] Logical_op,
  output [1:0] Comprator_op,
  output [1:0] Shifter_op,
  output [1:0] Alu_op
);

  wire and_1_out, and_2_out, and_3_out, and_4_out, and_6_out, and_7_out, and_8_out, and_9_out, and_10_out,
       and_11_out, and_12_out, and_13_out, and_14_out, and_15_out, and_16_out, and_17_out, not_1_out,
       not_2_out, not_3_out, not_4_out, not_5_out, not_6_out, not_7_out, not_8_out, not_9_out, not_10_out,
       not_12_out, not_13_out, not_14_out, not_15_out, not_17_out, not_18_out, not_19_out, not_20_out,
       not_21_out, not_22_out, not_23_out, not_24_out, not_25_out, not_26_out, not_27_out, not_28_out,
       not_29_out, not_30_out, not_31_out, not_32_out, not_33_out, not_34_out;
  wire [11:0] bit_extender_1_out;
  wire [11:1] multiplexer_1_out;

  assign bit_extender_1_out = {{6{1'b0}}, in_2};  // Bit_Extender bit_extender_1
  Multiplexer #(.width(12), .enable("false")) multiplexer_1 (
    .in0({1'b1, in_1}), .in1(bit_extender_1_out),
    .out({multiplexer_1_out[11:4], Arith_op[1], multiplexer_1_out[2:1], Comprator_op[1]}), .sel(in_3));
  not not_1 (not_1_out, multiplexer_1_out[11]);
  not not_2 (not_2_out, multiplexer_1_out[4]);
  not not_3 (not_3_out, Arith_op[1]);
  not not_4 (not_4_out, multiplexer_1_out[1]);
  not not_5 (not_5_out, Arith_op[1]);
  not not_6 (not_6_out, multiplexer_1_out[1]);
  not not_7 (not_7_out, Comprator_op[1]);
  not not_8 (not_8_out, Arith_op[1]);
  not not_9 (not_9_out, multiplexer_1_out[1]);
  not not_10 (not_10_out, Arith_op[1]);
  not not_11 (Logical_op[1], multiplexer_1_out[1]);
  not not_12 (not_12_out, multiplexer_1_out[2]);
  not not_13 (not_13_out, multiplexer_1_out[1]);
  not not_14 (not_14_out, multiplexer_1_out[2]);
  not not_15 (not_15_out, Comprator_op[1]);
  not not_16 (Comprator_op[0], multiplexer_1_out[2]);
  and and_1 (and_1_out, multiplexer_1_out[1], Comprator_op[1]);
  and and_2 (and_2_out, multiplexer_1_out[11], multiplexer_1_out[1]);
  not not_17 (not_17_out, multiplexer_1_out[11]);
  not not_18 (not_18_out, Comprator_op[1]);
  not not_19 (not_19_out, multiplexer_1_out[11]);
  not not_20 (not_20_out, multiplexer_1_out[4]);
  not not_21 (not_21_out, Arith_op[1]);
  not not_22 (not_22_out, Comprator_op[1]);
  not not_23 (not_23_out, multiplexer_1_out[4]);
  not not_24 (not_24_out, Arith_op[1]);
  not not_25 (not_25_out, multiplexer_1_out[2]);
  not not_26 (not_26_out, multiplexer_1_out[4]);
  not not_27 (not_27_out, multiplexer_1_out[2]);
  not not_28 (not_28_out, multiplexer_1_out[1]);
  not not_29 (not_29_out, Comprator_op[1]);
  not not_30 (not_30_out, Arith_op[1]);
  not not_31 (not_31_out, Arith_op[1]);
  not not_32 (not_32_out, multiplexer_1_out[2]);
  not not_33 (not_33_out, multiplexer_1_out[1]);
  not not_34 (not_34_out, Comprator_op[1]);
  and and_3 (and_3_out, not_1_out, not_2_out, not_3_out, multiplexer_1_out[2], not_4_out, Comprator_op[1]);
  and and_4 (and_4_out, not_5_out, not_6_out);
  and and_5 (Signal_of_sub, not_8_out, not_9_out);
  or or_1 (Arith_op[0], multiplexer_1_out[1], and_6_out);
  and and_6 (and_6_out, multiplexer_1_out[11], not_10_out, Comprator_op[1]);
  and and_7 (and_7_out, not_12_out, not_13_out);
  or or_2 (Logical_op[0], and_7_out, and_8_out);
  and and_8 (and_8_out, not_14_out, not_15_out);
  or or_3 (Shifter_op[1], and_1_out, multiplexer_1_out[2], and_2_out);
  and and_9 (and_9_out, not_17_out, not_18_out);
  or or_4 (Shifter_op[0], and_9_out, and_10_out);
  and and_10 (and_10_out, multiplexer_1_out[11], Comprator_op[1]);
  and and_11 (and_11_out, not_19_out, not_20_out, not_21_out, not_22_out);
  and and_12 (and_12_out, not_23_out, not_24_out, not_25_out);
  and and_13 (and_13_out, not_26_out, not_27_out, not_28_out, not_29_out);
  and and_14 (and_14_out, not_30_out, multiplexer_1_out[1]);
  and and_15 (and_15_out, not_31_out, multiplexer_1_out[2], multiplexer_1_out[1]);
  and and_16 (and_16_out, Arith_op[1], not_32_out);
  or or_5 (Alu_op[0], and_15_out, and_16_out, and_17_out);
  and and_17 (and_17_out, Arith_op[1], not_33_out, not_34_out);
  or or_6 (Signal_of_add, and_3_out, and_4_out);
  or or_7 (Alu_op[1], and_11_out, and_12_out, and_13_out, and_14_out);
endmodule
