// Logisim project PC.circ as structural Verilog: 1 circuit, main circuit main
module main (
  input  [31:0] in_1,
  input  [10:0] in_2,
  input  [15:0] in_3,
  input  in_4,
  input  [4:0] in_5,
  input  in_6,
  input  in_7,
  output [31:0] out_8
);

  wire adder_2_cout;
  wire [19:0] adder_2_out, adder_4_out, bit_extender_2_out, bit_extender_3_out, multiplexer_1_out,
       multiplexer_2_out, PC_11, PC_Register_q;

  assign out_8 = {{12{1'b0}}, PC_11};  // Bit_Extender bit_extender_1
  Register #(.width(20)) PC_Register (.D(multiplexer_2_out), .en(1'b1), .clk(in_4), .Q(PC_Register_q));  // open: clr
  assign bit_extender_2_out = {{4{in_2[10]}}, {in_2, in_5}};  // Bit_Extender bit_extender_2
  Adder #(.width(20)) adder_1 (.a(PC_Register_q), .b(20'h1), .out(PC_11), .cin(1'b0));  // open: cout
  Adder #(.width(20)) adder_2 (
    .a(PC_Register_q), .b(bit_extender_2_out), .out(adder_2_out), .cin(1'b0), .cout(adder_2_cout));
  Adder #(.width(20)) adder_3 (
    .a(PC_Register_q), .b(bit_extender_2_out), .out(adder_2_out), .cin(1'b0), .cout(adder_2_cout));
  assign bit_extender_3_out = {{4{in_3[15]}}, in_3};  // Bit_Extender bit_extender_3
  Adder #(.width(20)) adder_4 (.a(bit_extender_3_out), .b(in_1[19:0]), .out(adder_4_out), .cin(1'b0));  // open: cout
  Multiplexer #(.width(20), .enable("false")) multiplexer_1 (
    .in0(PC_11), .in1(adder_2_out), .out(multiplexer_1_out), .sel(in_6));
  Multiplexer #(.width(20), .enable("false")) multiplexer_2 (
    .in0(multiplexer_1_out), .in1(adder_4_out), .out(multiplexer_2_out), .sel(in_7));

  // Other names for the same wires on the sheet: ImmL[4:0] = in_5; ImmU[10:0] = in_2; clock = in_4;
  //   Imm16[15:0] = in_3; PC_1[31:0] = out_8; RS1[31:0] = in_1
endmodule
