// Logisim project data_memory.circ as structural Verilog: 1 circuit, main circuit main
module main (
  input  in_1,
  input  in_2,
  input  in_3,
  input  [31:0] in_4,
  input  [31:0] in_5,
  output [31:0] out_6
);

  wire not_1_out;

  not not_1 (not_1_out, in_2);
  RAM #(.addrWidth(20), .dataWidth(32), .databus("bibus")) ram_1 (
    .addr(in_5[19:0]), .we(in_3), .oe(in_1), .clk(not_1_out), .din(in_4), .dout(out_6));

  // Other names for the same wires on the sheet: Address[31:0] = in_5; clock = in_2; Data_in[31:0] = in_4;
  //   Data_out[31:0] = out_6; memRead = in_1; memWrite = in_3
endmodule
