// Logisim project Single_RISC_Processor.circ as structural Verilog: 1 circuit, main circuit main
module main (
  output [31:0] out_1,
  output [31:0] out_2,
  output [31:0] out_3,
  output [31:0] out_4,
  output [31:0] out_5,
  output [31:0] out_6,
  output [31:0] out_7,
  output [31:0] out_8,
  output [31:0] out_9,
  output [31:0] out_10,
  output [31:0] out_11,
  output [31:0] out_12,
  output [31:0] out_13,
  output [31:0] out_14,
  output [31:0] out_15,
  output [31:0] out_16,
  output [31:0] out_17,
  output [31:0] out_18,
  output [31:0] out_19,
  output [31:0] out_20,
  output [31:0] out_21,
  output [31:0] out_22,
  output [31:0] out_23,
  output [31:0] out_24,
  output [31:0] out_25,
  output [31:0] out_26,
  output [31:0] out_27,
  output [31:0] out_28,
  output [31:0] out_29,
  output [31:0] out_30,
  output [31:0] out_31,
  output [31:0] out_32,
  output [19:0] out_33
);

  wire ALU_ctrl, BEQ_BNE, BGEU, BLT, BLTU, BQE, Branch, CLK, JALR, main_7_out_12, Mem_Read, MemWrite,
       MUX_Extender, MUX_RD_2, MUX_SA_RS2, RegWrite, Signal_OF_ADD, Signal_OF_SUB;
  wire [1:0] ALU_op, Arith_op, Comparator_op, Logical_op, MUX_RD_1, MUX_S2_or_Imm16, Shifter_op;
  wire [4:0] main_3_p5, multiplexer_3_out, RD, RS_0_4, S1, SA;
  wire [5:0] Opcode;
  wire [10:0] ImmU_F;
  wire [15:0] RD_0_15;
  wire [15:5] SSET;
  wire [19:0] main_1_p9;
  wire [31:0] bit_extender_3_out, BusD, main_7_out_13, main_8_out_6, multiplexer_1_out, multiplexer_2_out,
       multiplexer_4_out, PC_1, RS1_value, RS2, SET, SW;

  assign BusD = JALR ? PC_1 : 32'bz;  // Controlled_Buffer controlled_buffer_1
  // PC_main main_1: pin names not known; wires that end beside it: ImmU_F, RD, CLK, Branch, {SSET, SA}, JALR, RS1_value, out_33, main_1_p9
  PC_Control_Unit_main main_2 (
    .BEQ(BEQ_BNE), .in_2(Opcode), .BNQ(BEQ_BNE), .BLT(BLT), .BGE(BQE), .BLTU(BLTU), .BGEU(BGEU), .JALR(JALR),
    .Branch(Branch));
  assign PC_1 = {{12{1'b0}}, main_1_p9};  // Bit_Extender bit_extender_1
  // Inst_memory_main main_3: pin names not known; wires that end beside it: out_33, Opcode, RD, S1, main_3_p5, ImmU_F, {SSET, SA}
  assign SET = {{16{SSET[15]}}, {SSET, SA}};  // Bit_Extender bit_extender_2
  assign bit_extender_3_out = {{16{1'b0}}, {SSET, SA}};  // Bit_Extender bit_extender_3
  Main_Control_Unit_main main_4 (
    .in_1(Opcode), .RegWrite(RegWrite), .MUX_Extender(MUX_Extender), .MUX_S2_or_Imm16(MUX_S2_or_Imm16),
    .MUX_RD_1(MUX_RD_1), .MUX_SA_RS2(MUX_SA_RS2), .MUX_RD_2(MUX_RD_2), .MemRead(Mem_Read),
    .MemWrite(MemWrite), .ALUctrl(ALU_ctrl));
  Multiplexer #(.width(32), .enable("false")) multiplexer_1 (
    .in0(SET), .in1(bit_extender_3_out), .out(multiplexer_1_out), .sel(MUX_Extender));
  assign SW = {{16{ImmU_F[10]}}, {ImmU_F, RD}};  // Bit_Extender bit_extender_4
  RF_main main_5 (
    .RW(RD), .RA(S1), .RB(main_3_p5), .in_6(CLK), .out_9(RS1_value), .out_10(RS2), .in_4(BusD),
    .in_5(RegWrite), .out_11(out_1), .out_12(out_2), .out_13(out_3), .out_14(out_4), .out_15(out_5),
    .out_16(out_6), .out_17(out_7), .out_18(out_8), .out_27(out_17), .out_28(out_18), .out_29(out_19),
    .out_30(out_20), .out_31(out_21), .out_32(out_22), .out_33(out_23), .out_34(out_24), .out_19(out_9),
    .out_20(out_10), .out_21(out_11), .out_22(out_12), .out_23(out_13), .out_24(out_14), .out_25(out_15),
    .out_26(out_16), .out_35(out_25), .out_36(out_26), .out_37(out_27), .out_38(out_28), .out_39(out_29),
    .out_40(out_30), .out_41(out_31), .out_42(out_32), .out_43(RS_0_4), .out_44(RD_0_15), .in_8(RD),
    .in_7(main_3_p5));
  ALU_control_unit_main main_6 (
    .in_1(ImmU_F), .in_2(Opcode), .Signal_of_add(Signal_OF_ADD), .Signal_of_sub(Signal_OF_SUB),
    .Arith_op(Arith_op), .Logical_op(Logical_op), .Comprator_op(Comparator_op), .Shifter_op(Shifter_op),
    .Alu_op(ALU_op), .in_3(ALU_ctrl));
  Multiplexer #(.select(2), .width(32), .enable("false")) multiplexer_2 (
    .in0(RS2), .in1(multiplexer_1_out), .in2(SW), .out(multiplexer_2_out), .sel(MUX_S2_or_Imm16));  // open: in3
  Multiplexer #(.width(5), .enable("false")) multiplexer_3 (
    .in0(SA), .in1(RS_0_4), .out(multiplexer_3_out), .sel(MUX_SA_RS2));
  // Probe on main_7_out_12
  ALU_main main_7 (
    .out_11(BLT), .out_14(BLTU), .out_16(BQE), .out_17(BGEU), .in_1(RS1_value), .in_2(multiplexer_2_out),
    .in_3(multiplexer_3_out), .in_4(Signal_OF_ADD), .in_5(Signal_OF_SUB), .out_12(main_7_out_12),
    .in_6(Arith_op), .in_7(Logical_op), .in_8(Shifter_op), .in_9(Comparator_op), .in_10(ALU_op),
    .out_13(main_7_out_13), .out_15(BEQ_BNE));
  // Probe on out_1
  // Probe on out_12
  // Probe on out_23
  // Probe on out_2
  // Probe on out_13
  // Probe on out_24
  // Probe on out_3
  // Probe on out_14
  // Probe on out_25
  // Probe on out_4
  // Probe on out_15
  // Probe on out_26
  // Probe on out_5
  // Probe on out_16
  // Probe on out_27
  // Probe on out_6
  // Probe on out_17
  // Probe on out_28
  data_memory_main main_8 (
    .in_2(CLK), .in_3(MemWrite), .in_4(RS2), .in_1(Mem_Read), .in_5(main_7_out_13), .out_6(main_8_out_6));
  // Probe on out_7
  // Probe on out_18
  // Probe on out_29
  // Probe on out_8
  // Probe on out_19
  // Probe on out_30
  Multiplexer #(.select(2), .width(32), .enable("false")) multiplexer_4 (
    .in0(main_7_out_13), .in1(main_8_out_6), .in2(SET), .in3({RD_0_15, SSET, SA}), .out(multiplexer_4_out),
    .sel(MUX_RD_1));
  // Probe on out_9
  // Probe on out_20
  // Probe on out_31
  // Probe on out_10
  // Probe on out_21
  // Probe on out_32
  Multiplexer #(.width(32), .enable("false")) multiplexer_5 (
    .in0(multiplexer_4_out), .in1(PC_1), .out(BusD), .sel(MUX_RD_2));
  // Probe on out_11
  // Probe on out_22
  Clock clock_1 (.out(CLK));

  // Other names for the same wires on the sheet: PC[19:0] = out_33; R0[31:0] = out_1; R1[31:0] = out_2;
  //   R2[31:0] = out_3; R3[31:0] = out_4; R4[31:0] = out_5; R5[31:0] = out_6; R6[31:0] = out_7; R7[31:0] = out_8;
  //   R8[31:0] = out_9; R9[31:0] = out_10; R10[31:0] = out_11; R11[31:0] = out_12; R12[31:0] = out_13;
  //   R13[31:0] = out_14; R14[31:0] = out_15; R15[31:0] = out_16; R16[31:0] = out_17; R17[31:0] = out_18;
  //   R18[31:0] = out_19; R19[31:0] = out_20; R20[31:0] = out_21; R21[31:0] = out_22; R22[31:0] = out_23;
  //   R23[31:0] = out_24; R24[31:0] = out_25; R25[31:0] = out_26; R26[31:0] = out_27; R27[31:0] = out_28;
  //   R28[31:0] = out_29; R29[31:0] = out_30; R30[31:0] = out_31; R31[31:0] = out_32;
  //   SSET (some bits) = {RD_0_15, SA}
endmodule
